// Logisim project ALU_Components.circ as structural Verilog: 6 circuits, main circuit Adder1bit
module Adder1bit (
  input  X,
  input  Y,
  input  Z,
  output S,
  output Co
);

  wire and_1_out, and_2_out, xor_1_out;

  xor xor_1 (xor_1_out, X, Y);
  and and_1 (and_1_out, X, Y);
  xor xor_2 (S, xor_1_out, Z);
  and and_2 (and_2_out, xor_1_out, Z);
  or or_1 (Co, and_2_out, and_1_out);
endmodule

module Adder4bit (
  input  [3:0] X,
  input  [3:0] Y,
  input  in_3,
  output [3:0] out_4,
  output out_5
);

  wire adder1bit_2_co, adder1bit_3_co, adder1bit_5_co;

  Adder1bit adder1bit_1 (.X(X[3]), .Y(Y[3]), .Z(adder1bit_2_co), .S(out_4[3]), .Co(out_5));
  Adder1bit adder1bit_2 (.X(X[2]), .Y(Y[2]), .Z(adder1bit_3_co), .S(out_4[2]), .Co(adder1bit_2_co));
  Adder1bit adder1bit_3 (.X(X[1]), .Y(Y[1]), .Z(adder1bit_5_co), .S(out_4[1]), .Co(adder1bit_3_co));
  Adder1bit adder1bit_4 (.X(X[1]), .Y(Y[1]), .Z(adder1bit_5_co), .S(out_4[1]), .Co(adder1bit_3_co));
  Adder1bit adder1bit_5 (.X(X[0]), .Y(Y[0]), .Z(in_3), .S(out_4[0]), .Co(adder1bit_5_co));
endmodule

module UnsignedSubtractor1bit (
  input  A,
  input  B,
  input  Bin,
  output D,
  output Bout
);

  wire and_1_out, and_2_out, not_1_out, not_2_out, xor_1_out;

  not not_1 (not_1_out, A);
  xor xor_1 (xor_1_out, A, B);
  and and_1 (and_1_out, not_1_out, B);
  not not_2 (not_2_out, xor_1_out);
  xor xor_2 (D, xor_1_out, Bin);
  and and_2 (and_2_out, not_2_out, Bin);
  or or_1 (Bout, and_2_out, and_1_out);
endmodule

module UnsignedSubtractor4bit (
  input  [3:0] A,
  input  [3:0] B,
  input  in_3,
  output [3:0] D,
  output BR4
);

  wire unsignedsubtractor1bit_2_bout, unsignedsubtractor1bit_3_bout, unsignedsubtractor1bit_4_bout;

  UnsignedSubtractor1bit unsignedsubtractor1bit_1 (
    .A(A[3]), .B(B[3]), .Bin(unsignedsubtractor1bit_2_bout), .D(D[3]), .Bout(BR4));
  UnsignedSubtractor1bit unsignedsubtractor1bit_2 (
    .A(A[2]), .B(B[2]), .Bin(unsignedsubtractor1bit_3_bout), .D(D[2]), .Bout(unsignedsubtractor1bit_2_bout));
  UnsignedSubtractor1bit unsignedsubtractor1bit_3 (
    .A(A[1]), .B(B[1]), .Bin(unsignedsubtractor1bit_4_bout), .D(D[1]), .Bout(unsignedsubtractor1bit_3_bout));
  UnsignedSubtractor1bit unsignedsubtractor1bit_4 (
    .A(A[0]), .B(B[0]), .Bin(in_3), .D(D[0]), .Bout(unsignedsubtractor1bit_4_bout));
endmodule

module SignedSubtractor4bit (
  input  [3:0] X,
  input  [3:0] Y,
  output [3:0] out_3,
  output out_4
);

  wire adder1bit_2_co, adder1bit_3_co, adder1bit_5_co, not_1_out, not_2_out, not_3_out, not_4_out,
       pull_resistor_1_node;

  not not_1 (not_1_out, Y[3]);
  Adder1bit adder1bit_1 (.X(X[3]), .Y(not_1_out), .Z(adder1bit_2_co), .S(out_3[3]), .Co(out_4));
  not not_2 (not_2_out, Y[2]);
  Adder1bit adder1bit_2 (.X(X[2]), .Y(not_2_out), .Z(adder1bit_3_co), .S(out_3[2]), .Co(adder1bit_2_co));
  not not_3 (not_3_out, Y[1]);
  Adder1bit adder1bit_3 (.X(X[1]), .Y(not_3_out), .Z(adder1bit_5_co), .S(out_3[1]), .Co(adder1bit_3_co));
  Adder1bit adder1bit_4 (.X(X[1]), .Y(not_3_out), .Z(adder1bit_5_co), .S(out_3[1]), .Co(adder1bit_3_co));
  not not_4 (not_4_out, Y[0]);
  Adder1bit adder1bit_5 (.X(X[0]), .Y(not_4_out), .Z(pull_resistor_1_node), .S(out_3[0]), .Co(adder1bit_5_co));
  Pull_Resistor #(.pull(1)) pull_resistor_1 (.node(pull_resistor_1_node));
endmodule

module SignedAdderSubtractor (
  input  [3:0] X,
  input  [3:0] Y,
  input  in_3,
  output [3:0] out_4,
  output out_5
);

  wire adder1bit_2_co, adder1bit_3_co, adder1bit_5_co, xor_1_out, xor_2_out, xor_3_out, xor_4_out;

  xor xor_1 (xor_1_out, Y[3], in_3);
  Adder1bit adder1bit_1 (.X(X[3]), .Y(xor_1_out), .Z(adder1bit_2_co), .S(out_4[3]), .Co(out_5));
  xor xor_2 (xor_2_out, Y[2], in_3);
  Adder1bit adder1bit_2 (.X(X[2]), .Y(xor_2_out), .Z(adder1bit_3_co), .S(out_4[2]), .Co(adder1bit_2_co));
  xor xor_3 (xor_3_out, Y[1], in_3);
  Adder1bit adder1bit_3 (.X(X[1]), .Y(xor_3_out), .Z(adder1bit_5_co), .S(out_4[1]), .Co(adder1bit_3_co));
  Adder1bit adder1bit_4 (.X(X[1]), .Y(xor_3_out), .Z(adder1bit_5_co), .S(out_4[1]), .Co(adder1bit_3_co));
  xor xor_4 (xor_4_out, Y[0], in_3);
  Adder1bit adder1bit_5 (.X(X[0]), .Y(xor_4_out), .Z(in_3), .S(out_4[0]), .Co(adder1bit_5_co));
endmodule
