// Logisim project FULL_ADDER.circ as structural Verilog: 2 circuits, main circuit Adder1bit
module Adder1bit (
  input  A,
  input  B,
  input  Cin,
  output S,
  output Co
);

  wire and_1_out, and_2_out, xor_1_out;

  xor xor_1 (xor_1_out, A, B);
  xor xor_2 (S, xor_1_out, Cin);
  and and_1 (and_1_out, xor_1_out, Cin);
  and and_2 (and_2_out, A, B);
  or or_1 (Co, and_1_out, and_2_out);
endmodule

module Adder4bit (
  input  [3:0] A,
  input  [3:0] B,
  input  in_3,
  output [4:0] out_4
);

  wire adder1bit_2_co, adder1bit_3_co, adder1bit_4_co;

  Adder1bit adder1bit_1 (.A(B[3]), .B(A[3]), .Cin(adder1bit_2_co), .S(out_4[3]), .Co(out_4[4]));
  Adder1bit adder1bit_2 (.A(B[2]), .B(A[2]), .Cin(adder1bit_3_co), .S(out_4[2]), .Co(adder1bit_2_co));
  Adder1bit adder1bit_3 (.A(B[1]), .B(A[1]), .Cin(adder1bit_4_co), .S(out_4[1]), .Co(adder1bit_3_co));
  Adder1bit adder1bit_4 (.A(B[0]), .B(A[0]), .Cin(in_3), .S(out_4[0]), .Co(adder1bit_4_co));
endmodule
