// Logisim project 2X3Ram.circ as structural Verilog: 3 circuits, main circuit SRAM_1x1
module SRAM_1x1 (
  input  Read_Select_1,
  input  Read_Select_2,
  input  Write_Data,
  input  Write_Select,
  input  Clock,
  output Read_Data_1,
  output Read_Data_2
);

  wire d_ff_1_q, multiplexer_1_out;

  Multiplexer multiplexer_1 (.in0(d_ff_1_q), .in1(Write_Data), .out(multiplexer_1_out), .sel(Write_Select));
  D_Flip_Flop d_ff_1 (.D(multiplexer_1_out), .clk(Clock), .Q(d_ff_1_q));  // open: Qn, preset, reset
  and and_1 (Read_Data_1, Read_Select_1, d_ff_1_q);
  and and_2 (Read_Data_2, Read_Select_2, d_ff_1_q);
endmodule

module SRAM_1x3 (
  input  Read_Select_1_153a9162,
  input  Read_Select_2_b7afe17a,
  input  Write_Select_92439ebd,
  input  [2:0] Write_Data_044f4f28,
  input  Clock,
  output [2:0] Read_Data_1_4896219d,
  output [2:0] Read_Date_2_3086c08c
);

  SRAM_1x1 sram_1x1_1 (
    .Write_Data(Write_Data_044f4f28[0]), .Write_Select(Write_Select_92439ebd), .Clock(Clock),
    .Read_Select_1(Read_Select_1_153a9162), .Read_Select_2(Read_Select_2_b7afe17a),
    .Read_Data_1(Read_Data_1_4896219d[0]), .Read_Data_2(Read_Date_2_3086c08c[0]));
  SRAM_1x1 sram_1x1_2 (
    .Write_Data(Write_Data_044f4f28[1]), .Write_Select(Write_Select_92439ebd), .Clock(Clock),
    .Read_Select_1(Read_Select_1_153a9162), .Read_Select_2(Read_Select_2_b7afe17a),
    .Read_Data_1(Read_Data_1_4896219d[1]), .Read_Data_2(Read_Data_1_4896219d[1]));
  SRAM_1x1 sram_1x1_3 (
    .Write_Data(Write_Data_044f4f28[2]), .Write_Select(Write_Select_92439ebd), .Clock(Clock),
    .Read_Select_1(Read_Select_1_153a9162), .Read_Select_2(Read_Select_2_b7afe17a),
    .Read_Data_1(Read_Data_1_4896219d[2]), .Read_Data_2(Read_Date_2_3086c08c[2]));

  assign Read_Date_2_3086c08c[1] = Read_Data_1_4896219d[1];
endmodule

module Ram2x3 (
  input  [2:0] Write_Data,
  input  Write_Enable,
  input  Write_Address_1,
  input  Read_Address1_Enable,
  input  Read_Address_1,
  input  Read_Address2_Enable,
  input  Read_Address_2,
  input  Clock,
  output [2:0] Read_Data_1,
  output [2:0] Read_Data_2
);

  wire R1_0, R1_1, R2_0, R2_1, W0, W1;
  wire [2:0] RD1_0, RD1_1, RD2_0, RD2_1;

  Decoder decoder_1 (.out0(W0), .out1(W1), .sel(Write_Address_1), .en(Write_Enable));
  Decoder decoder_2 (.out0(R1_0), .out1(R1_1), .sel(Read_Address_1), .en(Read_Address1_Enable));
  Decoder decoder_3 (.out0(R2_0), .out1(R2_1), .sel(Read_Address_2), .en(Read_Address2_Enable));
  SRAM_1x3 sram_1x3_1 (
    .Write_Data_044f4f28(Write_Data), .Clock(Clock), .Read_Select_2_b7afe17a(R2_0),
    .Write_Select_92439ebd(W0), .Read_Select_1_153a9162(R1_0), .Read_Data_1_4896219d(RD1_0),
    .Read_Date_2_3086c08c(RD2_0));
  SRAM_1x3 sram_1x3_2 (
    .Write_Data_044f4f28(Write_Data), .Clock(Clock), .Read_Select_2_b7afe17a(R2_1),
    .Write_Select_92439ebd(W1), .Read_Select_1_153a9162(R1_1), .Read_Data_1_4896219d(RD1_1),
    .Read_Date_2_3086c08c(RD2_1));
  assign Read_Data_1 = RD1_0 | RD1_1;  // OR_Gate or_1, 3 bits wide
  assign Read_Data_2 = RD2_0 | RD2_1;  // OR_Gate or_2, 3 bits wide
endmodule
