// Logisim project B_Final_2_.circ as structural Verilog: 15 circuits, main circuit ALU_Adder4bit
module ALU_Adder4bit (
  input  [3:0] A,
  input  [3:0] B,
  input  Sel,
  output CF,
  output [3:0] R
);

  wire alu_adder1bit_2_co, alu_adder1bit_3_co, alu_adder1bit_4_co, xor_1_out, xor_2_out, xor_3_out, xor_4_out;

  ALU_Adder1bit alu_adder1bit_1 (.A(A[3]), .B(xor_1_out), .Cin(alu_adder1bit_2_co), .S(R[3]), .Co(CF));
  xor xor_1 (xor_1_out, B[3], Sel);
  xor xor_2 (xor_2_out, B[2], Sel);
  ALU_Adder1bit alu_adder1bit_2 (.A(A[2]), .B(xor_2_out), .Cin(alu_adder1bit_3_co), .S(R[2]), .Co(alu_adder1bit_2_co));
  xor xor_3 (xor_3_out, B[1], Sel);
  ALU_Adder1bit alu_adder1bit_3 (.A(A[1]), .B(xor_3_out), .Cin(alu_adder1bit_4_co), .S(R[1]), .Co(alu_adder1bit_3_co));
  ALU_Adder1bit alu_adder1bit_4 (.A(A[0]), .B(xor_4_out), .Cin(Sel), .S(R[0]), .Co(alu_adder1bit_4_co));
  xor xor_4 (xor_4_out, B[0], Sel);
endmodule

module ALU_Adder1bit (
  input  A,
  input  B,
  input  Cin,
  output S,
  output Co
);

  wire and_1_out, and_2_out, xor_1_out;

  xor xor_1 (xor_1_out, A, B);
  and and_1 (and_1_out, B, A);
  xor xor_2 (S, xor_1_out, Cin);
  and and_2 (and_2_out, xor_1_out, Cin);
  or or_1 (Co, and_2_out, and_1_out);
endmodule

module ALU_LeftShifer4bit (
  input  [3:0] A,
  input  [1:0] B,
  output [3:0] out_3
);

  Multiplexer #(.select(2)) multiplexer_1 (.in0(A[3]), .in1(A[2]), .in2(A[1]), .in3(A[0]), .out(out_3[3]), .sel(B));
  Multiplexer #(.select(2)) multiplexer_2 (.in0(A[2]), .in1(A[1]), .in2(A[0]), .in3(A[3]), .out(out_3[2]), .sel(B));
  Multiplexer #(.select(2)) multiplexer_3 (.in0(A[1]), .in1(A[0]), .in2(A[3]), .in3(A[2]), .out(out_3[1]), .sel(B));
  Multiplexer #(.select(2)) multiplexer_4 (.in0(A[0]), .in1(A[3]), .in2(A[2]), .in3(A[1]), .out(out_3[0]), .sel(B));

  // Other names for the same wires on the sheet: R0 = out_3[0]; R1 = out_3[1]; R2 = out_3[2]; R3 = out_3[3];
  //   Shift[1:0] = B
endmodule

module ALU_ROL (
  input  [3:0] B,
  input  [3:0] A,
  output [3:0] R
);

  Multiplexer #(.select(2)) multiplexer_1 (.in0(A[3]), .in1(A[2]), .in2(A[1]), .in3(A[0]), .out(R[3]), .sel(B[1:0]));
  Multiplexer #(.select(2)) multiplexer_2 (.in0(A[2]), .in1(A[1]), .in2(A[0]), .in3(A[3]), .out(R[2]), .sel(B[1:0]));
  Multiplexer #(.select(2)) multiplexer_3 (.in0(A[1]), .in1(A[0]), .in2(A[3]), .in3(A[2]), .out(R[1]), .sel(B[1:0]));
  Multiplexer #(.select(2)) multiplexer_4 (.in0(A[0]), .in1(A[3]), .in2(A[2]), .in3(A[1]), .out(R[0]), .sel(B[1:0]));

  // Other names for the same wires on the sheet: Sel[1:0] = B[1:0]
endmodule

module RF_1bit (
  input  CLK,
  input  Din,
  input  Sel,
  output Dout
);

  wire multiplexer_1_out;

  D_Flip_Flop d_ff_1 (.clk(CLK), .D(multiplexer_1_out), .Q(Dout));  // open: Qn, preset, reset
  Multiplexer multiplexer_1 (.in0(Dout), .in1(Din), .out(multiplexer_1_out), .sel(Sel));
endmodule

module RF_4bit (
  input  [3:0] Din,
  input  Sel,
  input  CLK,
  output [3:0] Dout
);

  RF_1bit rf_1bit_1 (.CLK(CLK), .Din(Din[0]), .Sel(Sel), .Dout(Dout[0]));
  RF_1bit rf_1bit_2 (.CLK(CLK), .Din(Din[1]), .Sel(Sel), .Dout(Dout[1]));
  RF_1bit rf_1bit_3 (.CLK(CLK), .Din(Din[2]), .Sel(Sel), .Dout(Dout[2]));
  RF_1bit rf_1bit_4 (.CLK(CLK), .Din(Din[3]), .Sel(Sel), .Dout(Dout[3]));
endmodule

module RF_Set (
  input  [1:0] RA,
  input  [3:0] WRD,
  input  REG_EN,
  input  [1:0] WR,
  input  [3:0] InD,
  input  InE,
  input  CLK,
  input  [1:0] RB,
  output [3:0] A,
  output [3:0] R0,
  output [3:0] R1,
  output [3:0] R2,
  output [3:0] R3,
  output [3:0] OutD,
  output [3:0] B
);

  wire decoder_1_out0, decoder_1_out1, decoder_1_out3;

  Decoder #(.select(2)) decoder_1 (
    .out0(decoder_1_out0), .out1(decoder_1_out1), .out3(decoder_1_out3), .sel(WR), .en(REG_EN));  // open: out2
  RF_4bit rf_4bit_1 (.Sel(decoder_1_out0), .CLK(CLK), .Din(WRD), .Dout(R0));
  RF_4bit rf_4bit_2 (.Sel(decoder_1_out1), .CLK(CLK), .Din(WRD), .Dout(R1));
  RF_4bit rf_4bit_3 (.Sel(InE), .CLK(CLK), .Din(InD), .Dout(R2));
  RF_4bit rf_4bit_4 (.Sel(decoder_1_out3), .CLK(CLK), .Din(WRD), .Dout(OutD));
  Multiplexer #(.select(2), .width(4)) multiplexer_1 (.in0(R0), .in1(R1), .in2(R2), .in3(OutD), .out(A), .sel(RA));
  Multiplexer #(.select(2), .width(4)) multiplexer_2 (.in0(R0), .in1(R1), .in2(R2), .in3(OutD), .out(B), .sel(RB));

  assign R3 = OutD;
endmodule

module RAM_1x1 (
  input  Read_Select_1,
  input  CLK,
  input  Write_Data,
  input  Write_Sel,
  input  Read_Select_2,
  output Read_Data_1,
  output Read_Data_2,
  output Data
);

  wire multiplexer_1_out;

  D_Flip_Flop d_ff_1 (.clk(CLK), .D(multiplexer_1_out), .Q(Data));  // open: Qn, preset, reset
  Multiplexer multiplexer_1 (.in0(Data), .in1(Write_Data), .out(multiplexer_1_out), .sel(Write_Sel));
  and and_1 (Read_Data_1, Read_Select_1, Data);
  and and_2 (Read_Data_2, Data, Read_Select_2);
endmodule

module RAM_1x11 (
  input  RS1,
  input  RS2,
  input  WS,
  input  [10:0] WD,
  input  CLK,
  output [10:0] RD2,
  output [10:0] RD1,
  output [10:0] D
);

  RAM_1x1 ram_1x1_1 (
    .CLK(CLK), .Write_Data(WD[8]), .Write_Sel(WS), .Read_Select_1(RS1), .Read_Select_2(RS2),
    .Read_Data_1(RD1[8]), .Read_Data_2(RD2[8]), .Data(D[8]));
  RAM_1x1 ram_1x1_2 (
    .CLK(CLK), .Write_Data(WD[5]), .Write_Sel(WS), .Read_Select_1(RS1), .Read_Select_2(RS2),
    .Read_Data_1(RD1[5]), .Read_Data_2(RD2[5]), .Data(D[5]));
  RAM_1x1 ram_1x1_3 (
    .CLK(CLK), .Write_Data(WD[2]), .Write_Sel(WS), .Read_Select_1(RS1), .Read_Select_2(RS2),
    .Read_Data_1(RD1[2]), .Read_Data_2(RD2[2]), .Data(D[2]));
  RAM_1x1 ram_1x1_4 (
    .CLK(CLK), .Write_Data(WD[10]), .Write_Sel(WS), .Read_Select_1(RS1), .Read_Select_2(RS2),
    .Read_Data_1(RD1[10]), .Read_Data_2(RD2[10]), .Data(D[10]));
  RAM_1x1 ram_1x1_5 (
    .CLK(CLK), .Write_Data(WD[7]), .Write_Sel(WS), .Read_Select_1(RS1), .Read_Select_2(RS2),
    .Read_Data_1(RD1[7]), .Read_Data_2(RD2[7]), .Data(D[7]));
  RAM_1x1 ram_1x1_6 (
    .CLK(CLK), .Write_Data(WD[4]), .Write_Sel(WS), .Read_Select_1(RS1), .Read_Select_2(RS2),
    .Read_Data_1(RD1[4]), .Read_Data_2(RD2[4]), .Data(D[4]));
  RAM_1x1 ram_1x1_7 (
    .CLK(CLK), .Write_Data(WD[1]), .Write_Sel(WS), .Read_Select_1(RS1), .Read_Select_2(RS2),
    .Read_Data_1(RD1[1]), .Read_Data_2(RD2[1]), .Data(D[1]));
  RAM_1x1 ram_1x1_8 (
    .CLK(CLK), .Write_Data(WD[9]), .Write_Sel(WS), .Read_Select_1(RS1), .Read_Select_2(RS2),
    .Read_Data_1(RD1[9]), .Read_Data_2(RD2[9]), .Data(D[9]));
  RAM_1x1 ram_1x1_9 (
    .CLK(CLK), .Write_Data(WD[6]), .Write_Sel(WS), .Read_Select_1(RS1), .Read_Select_2(RS2),
    .Read_Data_1(RD1[6]), .Read_Data_2(RD2[6]), .Data(D[6]));
  RAM_1x1 ram_1x1_10 (
    .CLK(CLK), .Write_Data(WD[3]), .Write_Sel(WS), .Read_Select_1(RS1), .Read_Select_2(RS2),
    .Read_Data_1(RD1[3]), .Read_Data_2(RD2[3]), .Data(D[3]));
  RAM_1x1 ram_1x1_11 (
    .CLK(CLK), .Write_Data(WD[0]), .Write_Sel(WS), .Read_Select_1(RS1), .Read_Select_2(RS2),
    .Read_Data_1(RD1[0]), .Read_Data_2(RD2[0]), .Data(D[0]));

  // Other names for the same wires on the sheet: R1_0 = RD1[0]; R1_1 = RD1[1]; R1_2 = RD1[2]; R1_3 = RD1[3];
  //   R1_4 = RD1[4]; R1_5 = RD1[5]; R1_6 = RD1[6]; R1_7 = RD1[7]; R1_8 = RD1[8]; R1_9 = RD1[9]; R1_10 = RD1[10];
  //   R2_0 = RD2[0]; R2_1 = RD2[1]; R2_2 = RD2[2]; R2_3 = RD2[3]; R2_4 = RD2[4]; R2_5 = RD2[5]; R2_6 = RD2[6];
  //   R2_7 = RD2[7]; R2_8 = RD2[8]; R2_9 = RD2[9]; R2_10 = RD2[10]
endmodule

module RAM_8x11 (
  input  [2:0] RA1,
  input  [2:0] RA2,
  input  WE,
  input  [2:0] WA,
  input  [10:0] WD,
  input  CLK,
  output [10:0] RD1,
  output [10:0] RD2,
  output [10:0] D0,
  output [10:0] D1,
  output [10:0] D2,
  output [10:0] D3,
  output [10:0] D4,
  output [10:0] D5,
  output [10:0] D6,
  output [10:0] D7
);

  wire RA1_0, RA1_1, RA1_2, RA1_3, RA1_4, RA1_5, RA1_6, RA1_7, RA2_0, RA2_1, RA2_2, RA2_3, RA2_4, RA2_5,
       RA2_6, RA2_7, WD_0, WD_1, WD_2, WD_3, WD_4, WD_5, WD_6, WD_7;
  wire [10:0] ram_1x11_1_rd1, ram_1x11_1_rd2, ram_1x11_2_rd1, ram_1x11_2_rd2, ram_1x11_3_rd1, ram_1x11_3_rd2,
       ram_1x11_4_rd1, ram_1x11_4_rd2, ram_1x11_5_rd1, ram_1x11_5_rd2, ram_1x11_6_rd1, ram_1x11_6_rd2,
       ram_1x11_7_rd1, ram_1x11_7_rd2, ram_1x11_8_rd1, ram_1x11_8_rd2;

  Decoder #(.select(3)) decoder_1 (
    .out0(WD_0), .out1(WD_1), .out2(WD_2), .out3(WD_3), .out4(WD_4), .out5(WD_5), .out6(WD_6), .out7(WD_7),
    .sel(WA), .en(WE));
  Decoder #(.select(3)) decoder_2 (
    .out0(RA1_0), .out1(RA1_1), .out2(RA1_2), .out3(RA1_3), .out4(RA1_4), .out5(RA1_5), .out6(RA1_6),
    .out7(RA1_7), .sel(RA1));  // open: en
  Decoder #(.select(3)) decoder_3 (
    .out0(RA2_0), .out1(RA2_1), .out2(RA2_2), .out3(RA2_3), .out4(RA2_4), .out5(RA2_5), .out6(RA2_6),
    .out7(RA2_7), .sel(RA2));  // open: en
  RAM_1x11 ram_1x11_1 (
    .WD(WD), .RS1(RA1_0), .RS2(RA2_0), .WS(WD_0), .CLK(CLK), .D(D0), .RD1(ram_1x11_1_rd1),
    .RD2(ram_1x11_1_rd2));
  RAM_1x11 ram_1x11_2 (
    .WD(WD), .RS1(RA1_1), .RS2(RA2_1), .WS(WD_1), .CLK(CLK), .D(D1), .RD1(ram_1x11_2_rd1),
    .RD2(ram_1x11_2_rd2));
  RAM_1x11 ram_1x11_3 (
    .WD(WD), .RS1(RA1_2), .RS2(RA2_2), .WS(WD_2), .CLK(CLK), .D(D2), .RD1(ram_1x11_3_rd1),
    .RD2(ram_1x11_3_rd2));
  RAM_1x11 ram_1x11_4 (
    .WD(WD), .RS1(RA1_3), .RS2(RA2_3), .WS(WD_3), .CLK(CLK), .D(D3), .RD1(ram_1x11_4_rd1),
    .RD2(ram_1x11_4_rd2));
  RAM_1x11 ram_1x11_5 (
    .WD(WD), .RS1(RA1_4), .RS2(RA2_4), .WS(WD_4), .CLK(CLK), .D(D4), .RD1(ram_1x11_5_rd1),
    .RD2(ram_1x11_5_rd2));
  RAM_1x11 ram_1x11_6 (
    .WD(WD), .RS1(RA1_5), .RS2(RA2_5), .WS(WD_5), .CLK(CLK), .D(D5), .RD1(ram_1x11_6_rd1),
    .RD2(ram_1x11_6_rd2));
  RAM_1x11 ram_1x11_7 (
    .WD(WD), .RS1(RA1_6), .RS2(RA2_6), .WS(WD_6), .CLK(CLK), .D(D6), .RD1(ram_1x11_7_rd1),
    .RD2(ram_1x11_7_rd2));
  RAM_1x11 ram_1x11_8 (
    .WD(WD), .RS1(RA1_7), .RS2(RA2_7), .WS(WD_7), .CLK(CLK), .D(D7), .RD1(ram_1x11_8_rd1),
    .RD2(ram_1x11_8_rd2));
  assign RD1 = ram_1x11_1_rd1 | ram_1x11_2_rd1 | ram_1x11_3_rd1 | ram_1x11_4_rd1 | ram_1x11_5_rd1 | ram_1x11_6_rd1 | ram_1x11_7_rd1 | ram_1x11_8_rd1;  // OR_Gate or_1, 11 bits wide
  assign RD2 = ram_1x11_1_rd2 | ram_1x11_2_rd2 | ram_1x11_3_rd2 | ram_1x11_4_rd2 | ram_1x11_5_rd2 | ram_1x11_6_rd2 | ram_1x11_7_rd2 | ram_1x11_8_rd2;  // OR_Gate or_2, 11 bits wide
endmodule

module ALU_4bit (
  input  [3:0] A,
  input  [3:0] B,
  input  [1:0] Op,
  output SF,
  output ZF,
  output [3:0] R,
  output CF
);

  wire or_1_out, Sel;
  wire [3:0] ADD, RL;

  not not_1 (Sel, Op[0]);
  ALU_ROL alu_rol_1 (.B(B), .A(A), .R(RL));
  ALU_Adder4bit alu_adder4bit_1 (.Sel(Sel), .A(A), .B(B), .R(ADD), .CF(CF));
  Multiplexer #(.select(2), .width(4)) multiplexer_1 (.in0(ADD), .in2(RL), .in3(ADD), .out(R), .sel(Op));  // open: in1
  or or_1 (or_1_out, R[0], R[1], R[2], R[3]);
  not not_2 (ZF, or_1_out);

  assign SF = R[3];
endmodule

module PC (
  input  [2:0] I,
  input  CLK,
  output [2:0] O
);

  D_Flip_Flop d_ff_1 (.clk(CLK), .D(I[0]), .Q(O[0]));  // open: Qn, preset, reset
  D_Flip_Flop d_ff_2 (.clk(CLK), .D(I[1]), .Q(O[1]));  // open: Qn, preset, reset
  D_Flip_Flop d_ff_3 (.clk(CLK), .D(I[2]), .Q(O[2]));  // open: Qn, preset, reset
endmodule

module CU (
  input  [3:0] Opcode,
  input  ZF,
  input  SF,
  input  CF,
  output [1:0] OP,
  output REG_EN,
  output IMM_SEL,
  output JMP_SEL,
  output L_SEL
);

  wire and_1_out, CMP_out, DIR_out, FLAG_out, JGOP_out, JMP_out, MEM_out, or_1_out, or_2_out, RegM_out;

  and Imm (IMM_SEL, ~Opcode[3], Opcode[2]);  // AND_Gate
  and RegM (RegM_out, Opcode[3], ~Opcode[2]);  // AND_Gate
  and JMP (JMP_out, ~Opcode[3], ~Opcode[2]);  // AND_Gate
  and JGOP (JGOP_out, Opcode[1], Opcode[0]);
  and FLAG (FLAG_out, ~ZF, ~SF);  // AND_Gate
  and MEM (MEM_out, Opcode[0], Opcode[1]);
  and DIR (DIR_out, Opcode[2], Opcode[3]);
  or or_1 (or_1_out, IMM_SEL, RegM_out);
  and CMP (CMP_out, ~Opcode[1], ~Opcode[0]);  // AND_Gate
  and JG (JMP_SEL, JMP_out, JGOP_out, FLAG_out);
  and LDE (L_SEL, MEM_out, DIR_out);
  and and_1 (and_1_out, or_1_out, CMP_out);
  or or_2 (or_2_out, and_1_out, JMP_out);
  not not_1 (REG_EN, or_2_out);

  assign OP = Opcode[1:0];
endmodule

module FLAG_REG (
  input  ZF,
  input  SF,
  input  CF,
  input  CLK,
  output dZF,
  output dSF,
  output dCF
);

  D_Flip_Flop d_ff_1 (.clk(CLK), .D(ZF), .Q(dZF));  // open: Qn, preset, reset
  D_Flip_Flop d_ff_2 (.clk(CLK), .D(SF), .Q(dSF));  // open: Qn, preset, reset
  D_Flip_Flop d_ff_3 (.clk(CLK), .D(CF), .Q(dCF));  // open: Qn, preset, reset
endmodule

module CPU (
  input  [10:0] WD,
  input  [2:0] WA,
  input  WE,
  input  in_4,
  input  CLK,
  input  PC_Enable,
  output [3:0] REG0,
  output [10:0] RAM4,
  output [10:0] RAM0,
  output [3:0] REG1,
  output [3:0] REG2,
  output [10:0] RAM5,
  output [10:0] RAM1,
  output [3:0] REG3,
  output [10:0] RAM6,
  output [10:0] RAM2,
  output [10:0] RAM7,
  output [10:0] RAM3
);

  wire alu_4bit_1_cf, alu_4bit_1_sf, alu_4bit_1_zf, CPU_CLK, dCF, dSF, dZF, I_SEL, J_SEL, L_SEL, RE;
  wire [1:0] LD_ADD, OP;
  wire [2:0] adder_1_out, JMP_ADR, multiplexer_1_out, pc_1_o;
  wire [3:0] alu_4bit_1_r, InD, LD_DATA, multiplexer_2_out, multiplexer_3_out, OutD, rf_set_1_a, rf_set_1_b;
  wire [10:0] ram_8x11_1_rd1, ram_8x11_1_rd2;

  Multiplexer #(.width(3)) multiplexer_1 (.in0(adder_1_out), .in1(JMP_ADR), .out(multiplexer_1_out), .sel(J_SEL));
  Adder #(.width(3)) adder_1 (.a(pc_1_o), .b(3'b001), .out(adder_1_out));  // open: cin, cout
  PC pc_1 (.I(multiplexer_1_out), .CLK(CPU_CLK), .O(pc_1_o));
  and and_1 (CPU_CLK, CLK, PC_Enable);
  DipSwitch #(.number(4)) dipswitch_1 (.sw1(InD[3]), .sw2(InD[2]), .sw3(InD[1]), .sw4(InD[0]));
  RAM_8x11 ram_8x11_1 (
    .WE(WE), .WA(WA), .RA2({JMP_ADR[0], LD_ADD}), .RA1(pc_1_o), .WD(WD), .CLK(CLK),
    .RD1({ram_8x11_1_rd1[10:7], JMP_ADR, LD_ADD, ram_8x11_1_rd1[1:0]}),
    .RD2({ram_8x11_1_rd2[10:5], LD_DATA, ram_8x11_1_rd2[0]}), .D0(RAM0), .D1(RAM1), .D2(RAM2), .D3(RAM3),
    .D4(RAM4), .D5(RAM5), .D6(RAM6), .D7(RAM7));
  LED led_1 (.in(OutD[3]));
  LED led_2 (.in(OutD[2]));
  LED led_3 (.in(OutD[1]));
  LED led_4 (.in(OutD[0]));
  CU cu_1 (
    .ZF(dZF), .SF(dSF), .CF(dCF), .Opcode(ram_8x11_1_rd1[10:7]), .L_SEL(L_SEL), .OP(OP), .IMM_SEL(I_SEL),
    .JMP_SEL(J_SEL), .REG_EN(RE));
  FLAG_REG flag_reg_1 (
    .ZF(alu_4bit_1_zf), .SF(alu_4bit_1_sf), .CF(alu_4bit_1_cf), .CLK(CPU_CLK), .dZF(dZF), .dSF(dSF), .dCF(dCF));
  RF_Set rf_set_1 (
    .WRD(multiplexer_3_out), .REG_EN(RE), .WR(JMP_ADR[2:1]), .InD(InD), .InE(in_4), .CLK(CPU_CLK),
    .RA(JMP_ADR[2:1]), .RB({JMP_ADR[0], LD_ADD[1]}), .A(rf_set_1_a), .R0(REG0), .R1(REG1), .R2(REG2),
    .R3(REG3), .OutD(OutD), .B(rf_set_1_b));
  Multiplexer #(.width(4)) multiplexer_2 (
    .in0(rf_set_1_b), .in1({JMP_ADR[0], LD_ADD, ram_8x11_1_rd1[1]}), .out(multiplexer_2_out), .sel(I_SEL));
  ALU_4bit alu_4bit_1 (
    .Op(OP), .A(rf_set_1_a), .B(multiplexer_2_out), .SF(alu_4bit_1_sf), .R(alu_4bit_1_r), .CF(alu_4bit_1_cf),
    .ZF(alu_4bit_1_zf));
  Multiplexer #(.width(4)) multiplexer_3 (.in0(alu_4bit_1_r), .in1(LD_DATA), .out(multiplexer_3_out), .sel(L_SEL));

  // Other names for the same wires on the sheet: LD_ADD[2] = JMP_ADR[0]; D0[10:0] = RAM0; D1[10:0] = RAM1;
  //   D2[10:0] = RAM2; D3[10:0] = RAM3; D4[10:0] = RAM4; D5[10:0] = RAM5; D6[10:0] = RAM6; D7[10:0] = RAM7;
  //   InE = in_4; R0[3:0] = REG0; R1[3:0] = REG1; R2[3:0] = REG2; R3[3:0] = REG3
endmodule
