// Logisim project lab5_5bit_ST_Direct.circ as structural Verilog: 14 circuits, main circuit ALU_Adder5bit
module ALU_Adder5bit (
  input  [4:0] A,
  input  [4:0] B,
  input  Sel,
  output CF,
  output [4:0] R
);

  wire alu_adder1bit_2_co, alu_adder1bit_3_co, alu_adder1bit_4_co, alu_adder1bit_5_co, xor_1_out, xor_2_out,
       xor_3_out, xor_4_out, xor_5_out;

  xor xor_1 (xor_1_out, B[4], Sel);
  ALU_Adder1bit alu_adder1bit_1 (.A(A[4]), .B(xor_1_out), .Cin(alu_adder1bit_2_co), .S(R[4]), .Co(CF));
  xor xor_2 (xor_2_out, B[3], Sel);
  ALU_Adder1bit alu_adder1bit_2 (.A(A[3]), .B(xor_2_out), .Cin(alu_adder1bit_3_co), .S(R[3]), .Co(alu_adder1bit_2_co));
  ALU_Adder1bit alu_adder1bit_3 (.A(A[2]), .B(xor_3_out), .Cin(alu_adder1bit_4_co), .S(R[2]), .Co(alu_adder1bit_3_co));
  xor xor_3 (xor_3_out, B[2], Sel);
  xor xor_4 (xor_4_out, B[1], Sel);
  ALU_Adder1bit alu_adder1bit_4 (.A(A[1]), .B(xor_4_out), .Cin(alu_adder1bit_5_co), .S(R[1]), .Co(alu_adder1bit_4_co));
  xor xor_5 (xor_5_out, B[0], Sel);
  ALU_Adder1bit alu_adder1bit_5 (.A(A[0]), .B(xor_5_out), .Cin(Sel), .S(R[0]), .Co(alu_adder1bit_5_co));
endmodule

module ALU_Adder1bit (
  input  A,
  input  B,
  input  Cin,
  output S,
  output Co
);

  wire and_1_out, and_2_out, xor_1_out;

  xor xor_1 (xor_1_out, A, B);
  and and_1 (and_1_out, B, A);
  xor xor_2 (S, xor_1_out, Cin);
  and and_2 (and_2_out, xor_1_out, Cin);
  or or_1 (Co, and_2_out, and_1_out);
endmodule

module ALU_ROL_5bit (
  input  [4:0] A,
  input  [4:0] B,
  output [4:0] R
);

  Multiplexer #(.select(2)) multiplexer_1 (.in0(A[4]), .in1(A[3]), .in2(A[2]), .in3(A[1]), .out(R[4]), .sel(B[1:0]));
  Multiplexer #(.select(2)) multiplexer_2 (.in0(A[3]), .in1(A[2]), .in2(A[1]), .in3(A[0]), .out(R[3]), .sel(B[1:0]));
  Multiplexer #(.select(2)) multiplexer_3 (.in0(A[2]), .in1(A[1]), .in2(A[0]), .in3(A[4]), .out(R[2]), .sel(B[1:0]));
  Multiplexer #(.select(2)) multiplexer_4 (.in0(A[1]), .in1(A[0]), .in2(A[4]), .in3(A[3]), .out(R[1]), .sel(B[1:0]));
  Multiplexer #(.select(2)) multiplexer_5 (.in0(A[0]), .in1(A[4]), .in2(A[3]), .in3(A[2]), .out(R[0]), .sel(B[1:0]));

  // Other names for the same wires on the sheet: Sel[1:0] = B[1:0]
endmodule

module RF_1bit (
  input  CLK,
  input  Din,
  input  Sel,
  output Dout
);

  wire multiplexer_1_out;

  D_Flip_Flop d_ff_1 (.clk(CLK), .D(multiplexer_1_out), .Q(Dout));  // open: Qn, preset, reset
  Multiplexer multiplexer_1 (.in0(Dout), .in1(Din), .out(multiplexer_1_out), .sel(Sel));
endmodule

module RF_5bit (
  input  [4:0] Din,
  input  Sel,
  input  CLK,
  output [4:0] Dout
);

  RF_1bit rf_1bit_1 (.CLK(CLK), .Din(Din[4]), .Sel(Sel), .Dout(Dout[4]));
  RF_1bit rf_1bit_2 (.CLK(CLK), .Din(Din[3]), .Sel(Sel), .Dout(Dout[3]));
  RF_1bit rf_1bit_3 (.CLK(CLK), .Din(Din[2]), .Sel(Sel), .Dout(Dout[2]));
  RF_1bit rf_1bit_4 (.CLK(CLK), .Din(Din[1]), .Sel(Sel), .Dout(Dout[1]));
  RF_1bit rf_1bit_5 (.CLK(CLK), .Din(Din[0]), .Sel(Sel), .Dout(Dout[0]));
endmodule

module RF_Set (
  input  [1:0] RA,
  input  [4:0] WRD,
  input  REG_EN,
  input  [1:0] WR,
  input  [4:0] InD,
  input  InE,
  input  CLK,
  input  [1:0] RB,
  output [4:0] A,
  output [4:0] R0,
  output [4:0] R1,
  output [4:0] R2,
  output [4:0] R3,
  output [4:0] OutD,
  output [4:0] B
);

  wire decoder_1_out0, decoder_1_out1, decoder_1_out3;

  Decoder #(.select(2)) decoder_1 (
    .out0(decoder_1_out0), .out1(decoder_1_out1), .out3(decoder_1_out3), .sel(WR), .en(REG_EN));  // open: out2
  RF_5bit rf_5bit_1 (.Sel(decoder_1_out0), .CLK(CLK), .Din(WRD), .Dout(R0));
  RF_5bit rf_5bit_2 (.Sel(decoder_1_out1), .CLK(CLK), .Din(WRD), .Dout(R1));
  RF_5bit rf_5bit_3 (.Sel(InE), .CLK(CLK), .Din(InD), .Dout(R2));
  RF_5bit rf_5bit_4 (.Sel(decoder_1_out3), .CLK(CLK), .Din(WRD), .Dout(OutD));
  Multiplexer #(.select(2), .width(5)) multiplexer_1 (.in0(R0), .in1(R1), .in2(R2), .in3(OutD), .out(A), .sel(RA));
  Multiplexer #(.select(2), .width(5)) multiplexer_2 (.in0(R0), .in1(R1), .in2(R2), .in3(OutD), .out(B), .sel(RB));

  assign R3 = OutD;
endmodule

module RAM_1x1 (
  input  Read_Select_1,
  input  CLK,
  input  Write_Data,
  input  Write_Sel,
  input  Read_Select_2,
  output Read_Data_1,
  output Read_Data_2,
  output Data
);

  wire multiplexer_1_out;

  D_Flip_Flop d_ff_1 (.clk(CLK), .D(multiplexer_1_out), .Q(Data));  // open: Qn, preset, reset
  Multiplexer multiplexer_1 (.in0(Data), .in1(Write_Data), .out(multiplexer_1_out), .sel(Write_Sel));
  and and_1 (Read_Data_1, Read_Select_1, Data);
  and and_2 (Read_Data_2, Data, Read_Select_2);
endmodule

module RAM_1x11 (
  input  RS1,
  input  RS2,
  input  WS,
  input  [10:0] WD,
  input  CLK,
  output [10:0] RD2,
  output [10:0] RD1,
  output [10:0] D
);

  RAM_1x1 ram_1x1_1 (
    .CLK(CLK), .Write_Data(WD[8]), .Write_Sel(WS), .Read_Select_1(RS1), .Read_Select_2(RS2),
    .Read_Data_1(RD1[8]), .Read_Data_2(RD2[8]), .Data(D[8]));
  RAM_1x1 ram_1x1_2 (
    .CLK(CLK), .Write_Data(WD[5]), .Write_Sel(WS), .Read_Select_1(RS1), .Read_Select_2(RS2),
    .Read_Data_1(RD1[5]), .Read_Data_2(RD2[5]), .Data(D[5]));
  RAM_1x1 ram_1x1_3 (
    .CLK(CLK), .Write_Data(WD[2]), .Write_Sel(WS), .Read_Select_1(RS1), .Read_Select_2(RS2),
    .Read_Data_1(RD1[2]), .Read_Data_2(RD2[2]), .Data(D[2]));
  RAM_1x1 ram_1x1_4 (
    .CLK(CLK), .Write_Data(WD[10]), .Write_Sel(WS), .Read_Select_1(RS1), .Read_Select_2(RS2),
    .Read_Data_1(RD1[10]), .Read_Data_2(RD2[10]), .Data(D[10]));
  RAM_1x1 ram_1x1_5 (
    .CLK(CLK), .Write_Data(WD[7]), .Write_Sel(WS), .Read_Select_1(RS1), .Read_Select_2(RS2),
    .Read_Data_1(RD1[7]), .Read_Data_2(RD2[7]), .Data(D[7]));
  RAM_1x1 ram_1x1_6 (
    .CLK(CLK), .Write_Data(WD[4]), .Write_Sel(WS), .Read_Select_1(RS1), .Read_Select_2(RS2),
    .Read_Data_1(RD1[4]), .Read_Data_2(RD2[4]), .Data(D[4]));
  RAM_1x1 ram_1x1_7 (
    .CLK(CLK), .Write_Data(WD[1]), .Write_Sel(WS), .Read_Select_1(RS1), .Read_Select_2(RS2),
    .Read_Data_1(RD1[1]), .Read_Data_2(RD2[1]), .Data(D[1]));
  RAM_1x1 ram_1x1_8 (
    .CLK(CLK), .Write_Data(WD[9]), .Write_Sel(WS), .Read_Select_1(RS1), .Read_Select_2(RS2),
    .Read_Data_1(RD1[9]), .Read_Data_2(RD2[9]), .Data(D[9]));
  RAM_1x1 ram_1x1_9 (
    .CLK(CLK), .Write_Data(WD[6]), .Write_Sel(WS), .Read_Select_1(RS1), .Read_Select_2(RS2),
    .Read_Data_1(RD1[6]), .Read_Data_2(RD2[6]), .Data(D[6]));
  RAM_1x1 ram_1x1_10 (
    .CLK(CLK), .Write_Data(WD[3]), .Write_Sel(WS), .Read_Select_1(RS1), .Read_Select_2(RS2),
    .Read_Data_1(RD1[3]), .Read_Data_2(RD2[3]), .Data(D[3]));
  RAM_1x1 ram_1x1_11 (
    .CLK(CLK), .Write_Data(WD[0]), .Write_Sel(WS), .Read_Select_1(RS1), .Read_Select_2(RS2),
    .Read_Data_1(RD1[0]), .Read_Data_2(RD2[0]), .Data(D[0]));

  // Other names for the same wires on the sheet: R1_0 = RD1[0]; R1_1 = RD1[1]; R1_2 = RD1[2]; R1_3 = RD1[3];
  //   R1_4 = RD1[4]; R1_5 = RD1[5]; R1_6 = RD1[6]; R1_7 = RD1[7]; R1_8 = RD1[8]; R1_9 = RD1[9]; R1_10 = RD1[10];
  //   R2_0 = RD2[0]; R2_1 = RD2[1]; R2_2 = RD2[2]; R2_3 = RD2[3]; R2_4 = RD2[4]; R2_5 = RD2[5]; R2_6 = RD2[6];
  //   R2_7 = RD2[7]; R2_8 = RD2[8]; R2_9 = RD2[9]; R2_10 = RD2[10]
endmodule

module RAM_8x11 (
  input  [2:0] RA1,
  input  [2:0] RA2,
  input  WE,
  input  [2:0] WA,
  input  [10:0] WD,
  input  CLK,
  output [10:0] RD1,
  output [10:0] RD2,
  output [10:0] D0,
  output [10:0] D1,
  output [10:0] D2,
  output [10:0] D3,
  output [10:0] D4,
  output [10:0] D5,
  output [10:0] D6,
  output [10:0] D7
);

  wire RA1_0, RA1_1, RA1_2, RA1_3, RA1_4, RA1_5, RA1_6, RA1_7, RA2_0, RA2_1, RA2_2, RA2_3, RA2_4, RA2_5,
       RA2_6, RA2_7, WD_0, WD_1, WD_2, WD_3, WD_4, WD_5, WD_6, WD_7;
  wire [10:0] ram_1x11_1_rd1, ram_1x11_1_rd2, ram_1x11_2_rd1, ram_1x11_2_rd2, ram_1x11_3_rd1, ram_1x11_3_rd2,
       ram_1x11_4_rd1, ram_1x11_4_rd2, ram_1x11_5_rd1, ram_1x11_5_rd2, ram_1x11_6_rd1, ram_1x11_6_rd2,
       ram_1x11_7_rd1, ram_1x11_7_rd2, ram_1x11_8_rd1, ram_1x11_8_rd2;

  Decoder #(.select(3)) decoder_1 (
    .out0(RA1_0), .out1(RA1_1), .out2(RA1_2), .out3(RA1_3), .out4(RA1_4), .out5(RA1_5), .out6(RA1_6),
    .out7(RA1_7), .sel(RA1));  // open: en
  Decoder #(.select(3)) decoder_2 (
    .out0(RA2_0), .out1(RA2_1), .out2(RA2_2), .out3(RA2_3), .out4(RA2_4), .out5(RA2_5), .out6(RA2_6),
    .out7(RA2_7), .sel(RA2));  // open: en
  Decoder #(.select(3)) decoder_3 (
    .out0(WD_0), .out1(WD_1), .out2(WD_2), .out3(WD_3), .out4(WD_4), .out5(WD_5), .out6(WD_6), .out7(WD_7),
    .sel(WA), .en(WE));
  RAM_1x11 ram_1x11_1 (
    .CLK(CLK), .WD(WD), .RS1(RA1_0), .RS2(RA2_0), .WS(WD_0), .RD2(ram_1x11_1_rd2), .RD1(ram_1x11_1_rd1),
    .D(D0));
  RAM_1x11 ram_1x11_2 (
    .CLK(CLK), .WD(WD), .RS1(RA1_1), .RS2(RA2_1), .WS(WD_1), .RD2(ram_1x11_2_rd2), .RD1(ram_1x11_2_rd1),
    .D(D1));
  RAM_1x11 ram_1x11_3 (
    .CLK(CLK), .WD(WD), .RS1(RA1_2), .RS2(RA2_2), .WS(WD_2), .RD2(ram_1x11_3_rd2), .RD1(ram_1x11_3_rd1),
    .D(D2));
  RAM_1x11 ram_1x11_4 (
    .CLK(CLK), .WD(WD), .RS1(RA1_3), .RS2(RA2_3), .WS(WD_3), .RD2(ram_1x11_4_rd2), .RD1(ram_1x11_4_rd1),
    .D(D3));
  RAM_1x11 ram_1x11_5 (
    .CLK(CLK), .WD(WD), .RS1(RA1_4), .RS2(RA2_4), .WS(WD_4), .RD2(ram_1x11_5_rd2), .RD1(ram_1x11_5_rd1),
    .D(D4));
  RAM_1x11 ram_1x11_6 (
    .CLK(CLK), .WD(WD), .RS1(RA1_5), .RS2(RA2_5), .WS(WD_5), .RD2(ram_1x11_6_rd2), .RD1(ram_1x11_6_rd1),
    .D(D5));
  RAM_1x11 ram_1x11_7 (
    .CLK(CLK), .WD(WD), .RS1(RA1_6), .RS2(RA2_6), .WS(WD_6), .RD2(ram_1x11_7_rd2), .RD1(ram_1x11_7_rd1),
    .D(D6));
  RAM_1x11 ram_1x11_8 (
    .CLK(CLK), .WD(WD), .RS1(RA1_7), .RS2(RA2_7), .WS(WD_7), .RD2(ram_1x11_8_rd2), .RD1(ram_1x11_8_rd1),
    .D(D7));
  assign RD1 = ram_1x11_1_rd1 | ram_1x11_2_rd1 | ram_1x11_3_rd1 | ram_1x11_4_rd1 | ram_1x11_5_rd1 | ram_1x11_6_rd1 | ram_1x11_7_rd1 | ram_1x11_8_rd1;  // OR_Gate or_1, 11 bits wide
  assign RD2 = ram_1x11_1_rd2 | ram_1x11_2_rd2 | ram_1x11_3_rd2 | ram_1x11_4_rd2 | ram_1x11_5_rd2 | ram_1x11_6_rd2 | ram_1x11_7_rd2 | ram_1x11_8_rd2;  // OR_Gate or_2, 11 bits wide
endmodule

module ALU_5bit (
  input  [4:0] A,
  input  [4:0] B,
  input  [1:0] Op,
  output SF,
  output ZF,
  output [4:0] R,
  output CF
);

  wire or_1_out, Sel;
  wire [4:0] ADD, R_L;

  not not_1 (Sel, Op[0]);
  ALU_Adder5bit alu_adder5bit_1 (.Sel(Sel), .A(A), .B(B), .CF(CF), .R(ADD));
  ALU_ROL_5bit alu_rol_5bit_1 (.A(A), .B(B), .R(R_L));
  Multiplexer #(.select(2), .width(5)) multiplexer_1 (.in0(ADD), .in2(R_L), .in3(ADD), .out(R), .sel(Op));  // open: in1
  or or_1 (or_1_out, R[0], R[1], R[2], R[3], R[4]);
  not not_2 (ZF, or_1_out);

  assign SF = R[4];
endmodule

module PC (
  input  [2:0] I,
  input  CLK,
  output [2:0] O
);

  D_Flip_Flop d_ff_1 (.clk(CLK), .D(I[0]), .Q(O[0]));  // open: Qn, preset, reset
  D_Flip_Flop d_ff_2 (.clk(CLK), .D(I[1]), .Q(O[1]));  // open: Qn, preset, reset
  D_Flip_Flop d_ff_3 (.clk(CLK), .D(I[2]), .Q(O[2]));  // open: Qn, preset, reset
endmodule

module CU (
  input  [3:0] Opcode,
  input  ZF,
  input  SF,
  input  CF,
  output [1:0] OP,
  output REG_EN,
  output IMM_SEL,
  output JMP_SEL,
  output ST_SEL
);

  wire and_1_out, CMP_out, FLAG_out, JGOP_out, JMP_out, MEM_out, or_1_out, or_2_out, RegM_out, STOP_out;

  and Imm (IMM_SEL, ~Opcode[3], Opcode[2]);  // AND_Gate
  and RegM (RegM_out, Opcode[3], ~Opcode[2]);  // AND_Gate
  and JMP (JMP_out, ~Opcode[3], ~Opcode[2]);  // AND_Gate
  and JGOP (JGOP_out, Opcode[1], Opcode[0]);
  and FLAG (FLAG_out, ~ZF, ~SF);  // AND_Gate
  and MEM (MEM_out, Opcode[3], Opcode[2]);
  and STOP (STOP_out, ~Opcode[1], ~Opcode[0]);  // AND_Gate
  or or_1 (or_1_out, IMM_SEL, RegM_out);
  and CMP (CMP_out, ~Opcode[1], ~Opcode[0]);  // AND_Gate
  and JG (JMP_SEL, JMP_out, JGOP_out, FLAG_out);
  and and_1 (and_1_out, or_1_out, CMP_out);
  and ST (ST_SEL, MEM_out, STOP_out);
  or or_2 (or_2_out, and_1_out, JMP_out, ST_SEL);
  not not_1 (REG_EN, or_2_out);

  assign OP = Opcode[1:0];
endmodule

module FLAG_REG (
  input  ZF,
  input  SF,
  input  CF,
  input  CLK,
  output dZF,
  output dSF,
  output dCF
);

  D_Flip_Flop d_ff_1 (.clk(CLK), .D(ZF), .Q(dZF));  // open: Qn, preset, reset
  D_Flip_Flop d_ff_2 (.clk(CLK), .D(SF), .Q(dSF));  // open: Qn, preset, reset
  D_Flip_Flop d_ff_3 (.clk(CLK), .D(CF), .Q(dCF));  // open: Qn, preset, reset
endmodule

module CPU (
  input  [10:0] WD,
  input  [2:0] WA,
  input  WE,
  input  in_4,
  input  CLK,
  input  PC_Enable,
  output [4:0] REG0,
  output [10:0] RAM4,
  output [10:0] RAM0,
  output [4:0] REG1,
  output [4:0] REG2,
  output [10:0] RAM5,
  output [10:0] RAM1,
  output [4:0] REG3,
  output [10:0] RAM6,
  output [10:0] RAM2,
  output [10:0] RAM7,
  output [10:0] RAM3
);

  wire CF, CPU_CLK, dCF, dSF, dZF, I_SEL, J_SEL, or_1_out, RE, S_SEL, SF, ZF;
  wire [1:0] OP, ST_Ad;
  wire [2:0] adder_1_out, JMP_ADR, multiplexer_1_out, multiplexer_3_out, pc_1_o;
  wire [4:0] alu_5bit_1_r, InD, multiplexer_4_out, OutD, rf_set_1_b, S_DATA;
  wire [10:0] bit_extender_1_out, multiplexer_2_out, ram_8x11_1_rd1;

  Multiplexer #(.width(3)) multiplexer_1 (.in0(adder_1_out), .in1(JMP_ADR), .out(multiplexer_1_out), .sel(J_SEL));
  or or_1 (or_1_out, WE, S_SEL);
  assign bit_extender_1_out = {{6{1'b0}}, S_DATA};  // Bit_Extender bit_extender_1
  Adder #(.width(3)) adder_1 (.a(pc_1_o), .b(3'b001), .out(adder_1_out));  // open: cin, cout
  PC pc_1 (.I(multiplexer_1_out), .CLK(CPU_CLK), .O(pc_1_o));
  Multiplexer #(.width(11)) multiplexer_2 (.in0(WD), .in1(bit_extender_1_out), .out(multiplexer_2_out), .sel(S_SEL));
  Multiplexer #(.width(3)) multiplexer_3 (.in0(WA), .in1({JMP_ADR[0], ST_Ad}), .out(multiplexer_3_out));  // open: sel
  and and_1 (CPU_CLK, CLK, PC_Enable);
  DipSwitch #(.number(5)) dipswitch_1 (.sw1(InD[4]), .sw2(InD[3]), .sw3(InD[2]), .sw4(InD[1]), .sw5(InD[0]));
  LED led_1 (.in(OutD[4]));
  RAM_8x11 ram_8x11_1 (
    .WE(or_1_out), .WA(multiplexer_3_out), .RA1(pc_1_o), .WD(multiplexer_2_out), .CLK(CLK),
    .RD1({ram_8x11_1_rd1[10:7], JMP_ADR, ST_Ad, ram_8x11_1_rd1[1:0]}), .D0(RAM0), .D1(RAM1), .D2(RAM2),
    .D3(RAM3), .D4(RAM4), .D5(RAM5), .D6(RAM6), .D7(RAM7));  // open: RA2, RD2
  LED led_2 (.in(OutD[3]));
  LED led_3 (.in(OutD[2]));
  LED led_4 (.in(OutD[1]));
  LED led_5 (.in(OutD[0]));
  CU cu_1 (
    .ZF(dZF), .SF(dSF), .CF(dCF), .Opcode(ram_8x11_1_rd1[10:7]), .IMM_SEL(I_SEL), .JMP_SEL(J_SEL),
    .ST_SEL(S_SEL), .OP(OP), .REG_EN(RE));
  RF_Set rf_set_1 (
    .REG_EN(RE), .InE(in_4), .WR(JMP_ADR[2:1]), .WRD(alu_5bit_1_r), .InD(InD), .CLK(CPU_CLK),
    .RA(JMP_ADR[2:1]), .RB({JMP_ADR[0], ST_Ad[1]}), .A(S_DATA), .R0(REG0), .R1(REG1), .R2(REG2), .R3(REG3),
    .OutD(OutD), .B(rf_set_1_b));
  FLAG_REG flag_reg_1 (.ZF(ZF), .SF(SF), .CF(CF), .CLK(CPU_CLK), .dZF(dZF), .dSF(dSF), .dCF(dCF));
  Multiplexer #(.width(5)) multiplexer_4 (
    .in0(rf_set_1_b), .in1({JMP_ADR[0], ST_Ad, ram_8x11_1_rd1[1:0]}), .out(multiplexer_4_out), .sel(I_SEL));
  ALU_5bit alu_5bit_1 (.A(S_DATA), .B(multiplexer_4_out), .Op(OP), .CF(CF), .SF(SF), .R(alu_5bit_1_r), .ZF(ZF));

  // Other names for the same wires on the sheet: ST_Ad[2] = JMP_ADR[0]; D0[10:0] = RAM0; D1[10:0] = RAM1;
  //   D2[10:0] = RAM2; D3[10:0] = RAM3; D4[10:0] = RAM4; D5[10:0] = RAM5; D6[10:0] = RAM6; D7[10:0] = RAM7;
  //   InE = in_4; R0[4:0] = REG0; R1[4:0] = REG1; R2[4:0] = REG2; R3[4:0] = REG3
endmodule
