// Logisim project LPE2_2003154_Q2.circ as structural Verilog: 3 circuits, main circuit SRAM_1x1
module SRAM_1x1 (
  input  Read_Select,
  input  Write_Data,
  input  Write_Select,
  input  Clock,
  output Read_Data
);

  wire d_ff_1_q, multiplexer_1_out;

  Multiplexer multiplexer_1 (.in0(d_ff_1_q), .in1(Write_Data), .out(multiplexer_1_out), .sel(Write_Select));
  D_Flip_Flop d_ff_1 (.D(multiplexer_1_out), .clk(Clock), .Q(d_ff_1_q));  // open: Qn, preset, reset
  and and_1 (Read_Data, Read_Select, d_ff_1_q);
endmodule

module SRAM_1x3 (
  input  Read_Select,
  input  Write_Select,
  input  [2:0] Write_Data,
  input  Clock,
  output [2:0] Read_Data
);

  SRAM_1x1 sram_1x1_1 (
    .Write_Data(Write_Data[0]), .Write_Select(Write_Select), .Clock(Clock), .Read_Select(Read_Select),
    .Read_Data(Read_Data[0]));
  SRAM_1x1 sram_1x1_2 (
    .Write_Data(Write_Data[1]), .Write_Select(Write_Select), .Clock(Clock), .Read_Select(Read_Select),
    .Read_Data(Read_Data[1]));
  SRAM_1x1 sram_1x1_3 (
    .Write_Data(Write_Data[2]), .Write_Select(Write_Select), .Clock(Clock), .Read_Select(Read_Select),
    .Read_Data(Read_Data[2]));
endmodule

module Ram2x3 (
  input  [2:0] Write_Data,
  input  Write_Enable,
  input  Write_Address,
  input  Read_Address_Enable,
  input  Read_Address,
  input  Clock,
  output [2:0] Read_Data
);

  wire R_0, R_1, W0, W1;
  wire [2:0] RD1_0, RD1_1;

  Decoder decoder_1 (.out0(W0), .out1(W1), .sel(Write_Address), .en(Write_Enable));
  Decoder decoder_2 (.out0(R_0), .out1(R_1), .sel(Read_Address), .en(Read_Address_Enable));
  SRAM_1x3 sram_1x3_1 (.Write_Data(Write_Data), .Clock(Clock), .Write_Select(W0), .Read_Select(R_0), .Read_Data(RD1_0));
  SRAM_1x3 sram_1x3_2 (.Write_Data(Write_Data), .Clock(Clock), .Write_Select(W1), .Read_Select(R_1), .Read_Data(RD1_1));
  assign Read_Data = RD1_0 | RD1_1;  // OR_Gate or_1, 3 bits wide
endmodule
