// Logisim project RAM_library.circ as structural Verilog: 8 circuits, main circuit L_1x1_SRAM
module L_1x1_SRAM (
  input  Read_Select_1,
  input  Read_Select_2,
  input  Write_Data,
  input  Write_Select,
  input  Clock,
  output Read_Data_1,
  output Read_Data_2
);

  wire d_ff_1_q, multiplexer_1_out;

  Multiplexer multiplexer_1 (.in0(d_ff_1_q), .in1(Write_Data), .out(multiplexer_1_out), .sel(Write_Select));
  D_Flip_Flop d_ff_1 (.D(multiplexer_1_out), .clk(Clock), .Q(d_ff_1_q));  // open: Qn, preset, reset
  and and_1 (Read_Data_1, Read_Select_1, d_ff_1_q);
  and and_2 (Read_Data_2, Read_Select_2, d_ff_1_q);
endmodule

module L_1x3_SRAM (
  input  Read_Select_1_153a9162,
  input  Read_Select_2_b7afe17a,
  input  Write_Select_92439ebd,
  input  [2:0] Write_Data_044f4f28,
  input  Clock,
  output [2:0] Read_Data_1_4896219d,
  output [2:0] Read_Date_2_3086c08c
);

  L_1x1_SRAM l_1x1_sram_1 (
    .Write_Data(Write_Data_044f4f28[0]), .Write_Select(Write_Select_92439ebd), .Clock(Clock),
    .Read_Select_1(Read_Select_1_153a9162), .Read_Select_2(Read_Select_2_b7afe17a),
    .Read_Data_1(Read_Data_1_4896219d[0]), .Read_Data_2(Read_Date_2_3086c08c[0]));
  L_1x1_SRAM l_1x1_sram_2 (
    .Write_Data(Write_Data_044f4f28[1]), .Write_Select(Write_Select_92439ebd), .Clock(Clock),
    .Read_Select_1(Read_Select_1_153a9162), .Read_Select_2(Read_Select_2_b7afe17a),
    .Read_Data_1(Read_Data_1_4896219d[1]), .Read_Data_2(Read_Date_2_3086c08c[1]));
  L_1x1_SRAM l_1x1_sram_3 (
    .Write_Data(Write_Data_044f4f28[2]), .Write_Select(Write_Select_92439ebd), .Clock(Clock),
    .Read_Select_1(Read_Select_1_153a9162), .Read_Select_2(Read_Select_2_b7afe17a),
    .Read_Data_1(Read_Data_1_4896219d[2]), .Read_Data_2(Read_Date_2_3086c08c[2]));
endmodule

module L_1x13_SRAM (
  input  Read_Select_1_153a9162,
  input  Read_Select_2_b7afe17a,
  input  Write_Select_92439ebd,
  input  Clock,
  input  [12:0] Write_Data_044f4f28,
  output [12:0] Read_Data_1_12_0_a238470c,
  output [12:0] Read_Data_2_12_0_772128e8
);

  L_1x3_SRAM l_1x3_sram_1 (
    .Write_Data_044f4f28(Write_Data_044f4f28[12:10]), .Clock(Clock),
    .Read_Select_2_b7afe17a(Read_Select_2_b7afe17a), .Write_Select_92439ebd(Write_Select_92439ebd),
    .Read_Select_1_153a9162(Read_Select_1_153a9162), .Read_Data_1_4896219d(Read_Data_1_12_0_a238470c[12:10]),
    .Read_Date_2_3086c08c(Read_Data_2_12_0_772128e8[12:10]));
  L_1x3_SRAM l_1x3_sram_2 (
    .Write_Data_044f4f28(Write_Data_044f4f28[9:7]), .Clock(Clock),
    .Read_Select_2_b7afe17a(Read_Select_2_b7afe17a), .Write_Select_92439ebd(Write_Select_92439ebd),
    .Read_Select_1_153a9162(Read_Select_1_153a9162), .Read_Data_1_4896219d(Read_Data_1_12_0_a238470c[9:7]),
    .Read_Date_2_3086c08c(Read_Data_2_12_0_772128e8[9:7]));
  L_1x3_SRAM l_1x3_sram_3 (
    .Write_Data_044f4f28(Write_Data_044f4f28[6:4]), .Clock(Clock),
    .Read_Select_2_b7afe17a(Read_Select_2_b7afe17a), .Write_Select_92439ebd(Write_Select_92439ebd),
    .Read_Select_1_153a9162(Read_Select_1_153a9162), .Read_Data_1_4896219d(Read_Data_1_12_0_a238470c[6:4]),
    .Read_Date_2_3086c08c(Read_Data_2_12_0_772128e8[6:4]));
  L_1x3_SRAM l_1x3_sram_4 (
    .Write_Data_044f4f28(Write_Data_044f4f28[3:1]), .Clock(Clock),
    .Read_Select_2_b7afe17a(Read_Select_2_b7afe17a), .Write_Select_92439ebd(Write_Select_92439ebd),
    .Read_Select_1_153a9162(Read_Select_1_153a9162), .Read_Data_1_4896219d(Read_Data_1_12_0_a238470c[3:1]),
    .Read_Date_2_3086c08c(Read_Data_2_12_0_772128e8[3:1]));
  L_1x1_SRAM l_1x1_sram_1 (
    .Write_Data(Write_Data_044f4f28[0]), .Write_Select(Write_Select_92439ebd), .Clock(Clock),
    .Read_Select_1(Read_Select_1_153a9162), .Read_Select_2(Read_Select_2_b7afe17a),
    .Read_Data_1(Read_Data_1_12_0_a238470c[0]), .Read_Data_2(Read_Data_2_12_0_772128e8[0]));

  // Notes on the sheet:
  //   Write_Data_044f4f28: pull=down
endmodule

module L_4x13_SRAM (
  input  [12:0] Write_Data_12_0_6c18a168,
  input  Write_Enable_46f62da9,
  input  [1:0] Write_Address_1_0_5750fd8a,
  input  Read_Address1_Enable_996bc5a8,
  input  [1:0] Read_Address_1_1_0_b69a7a8d,
  input  Read_Address2_Enable_1a2e55ec,
  input  [1:0] Read_Address_2_1_0_ce9bad49,
  input  Clock,
  output [12:0] Read_Data_1_12_0_a238470c,
  output [12:0] Read_Data_2_12_0_772128e8
);

  wire R1_0, R1_1, R1_2, R1_3, R2_0, R2_1, R2_2, R2_3, W0, W1, W2, W3;
  wire [12:0] RD1_0, RD1_1, RD1_2, RD1_3, RD2_0, RD2_1, RD2_2, RD2_3;

  Decoder #(.select(2)) decoder_1 (
    .out0(W0), .out1(W1), .out2(W2), .out3(W3), .sel(Write_Address_1_0_5750fd8a), .en(Write_Enable_46f62da9));
  Decoder #(.select(2)) decoder_2 (
    .out0(R1_0), .out1(R1_1), .out2(R1_2), .out3(R1_3), .sel(Read_Address_1_1_0_b69a7a8d),
    .en(Read_Address1_Enable_996bc5a8));
  Decoder #(.select(2)) decoder_3 (
    .out0(R2_0), .out1(R2_1), .out2(R2_2), .out3(R2_3), .sel(Read_Address_2_1_0_ce9bad49),
    .en(Read_Address2_Enable_1a2e55ec));
  L_1x13_SRAM l_1x13_sram_1 (
    .Clock(Clock), .Read_Select_1_153a9162(R1_0), .Read_Select_2_b7afe17a(R2_0), .Write_Select_92439ebd(W0),
    .Write_Data_044f4f28(Write_Data_12_0_6c18a168), .Read_Data_1_12_0_a238470c(RD1_0),
    .Read_Data_2_12_0_772128e8(RD2_0));
  L_1x13_SRAM l_1x13_sram_2 (
    .Clock(Clock), .Read_Select_1_153a9162(R1_1), .Read_Select_2_b7afe17a(R2_1), .Write_Select_92439ebd(W1),
    .Write_Data_044f4f28(Write_Data_12_0_6c18a168), .Read_Data_1_12_0_a238470c(RD1_1),
    .Read_Data_2_12_0_772128e8(RD2_1));
  L_1x13_SRAM l_1x13_sram_3 (
    .Clock(Clock), .Read_Select_1_153a9162(R1_2), .Read_Select_2_b7afe17a(R2_2), .Write_Select_92439ebd(W2),
    .Write_Data_044f4f28(Write_Data_12_0_6c18a168), .Read_Data_1_12_0_a238470c(RD1_2),
    .Read_Data_2_12_0_772128e8(RD2_2));
  L_1x13_SRAM l_1x13_sram_4 (
    .Clock(Clock), .Read_Select_1_153a9162(R1_3), .Read_Select_2_b7afe17a(R2_3), .Write_Select_92439ebd(W3),
    .Write_Data_044f4f28(Write_Data_12_0_6c18a168), .Read_Data_1_12_0_a238470c(RD1_3),
    .Read_Data_2_12_0_772128e8(RD2_3));
  assign Read_Data_1_12_0_a238470c = RD1_0 | RD1_1 | RD1_2 | RD1_3;  // OR_Gate or_1, 13 bits wide
  assign Read_Data_2_12_0_772128e8 = RD2_0 | RD2_1 | RD2_2 | RD2_3;  // OR_Gate or_2, 13 bits wide
endmodule

module L_16x13_SRAM (
  input  [3:0] Read_Address_1_3_0_3886bda4,
  input  [3:0] Read_Address_2_3_0_9b81066c,
  input  Read_Address1_Enable_996bc5a8,
  input  Read_Address2_Enable_1a2e55ec,
  input  [3:0] Write_Address_3_0_fc297a62,
  input  [12:0] Write_Data_12_0_6c18a168,
  input  Write_Enable_46f62da9,
  input  Clock,
  output [12:0] Read_Data_1_12_0_a238470c,
  output [12:0] Read_Data_2_12_0_772128e8
);

  wire R1_0, R1_1, R1_2, R1_3, R2_0, R2_1, R2_2, R2_3, W0, W1, W2, W3;
  wire [12:0] RD1_0, RD1_1, RD1_2, RD1_3, RD2_0, RD2_1, RD2_2, RD2_3;

  Decoder #(.select(2)) decoder_1 (
    .out0(R1_0), .out1(R1_1), .out2(R1_2), .out3(R1_3), .sel(Read_Address_1_3_0_3886bda4[3:2]),
    .en(Read_Address1_Enable_996bc5a8));
  Decoder #(.select(2)) decoder_2 (
    .out0(R2_0), .out1(R2_1), .out2(R2_2), .out3(R2_3), .sel(Read_Address_2_3_0_9b81066c[3:2]),
    .en(Read_Address2_Enable_1a2e55ec));
  Decoder #(.select(2)) decoder_3 (
    .out0(W0), .out1(W1), .out2(W2), .out3(W3), .sel(Write_Address_3_0_fc297a62[3:2]),
    .en(Write_Enable_46f62da9));
  L_4x13_SRAM l_4x13_sram_1 (
    .Write_Data_12_0_6c18a168(Write_Data_12_0_6c18a168), .Write_Enable_46f62da9(W0),
    .Write_Address_1_0_5750fd8a(Write_Address_3_0_fc297a62[1:0]),
    .Read_Address_1_1_0_b69a7a8d(Read_Address_1_3_0_3886bda4[1:0]), .Read_Address2_Enable_1a2e55ec(R2_0),
    .Read_Address_2_1_0_ce9bad49(Read_Address_2_3_0_9b81066c[1:0]), .Clock(Clock),
    .Read_Address1_Enable_996bc5a8(R1_0), .Read_Data_1_12_0_a238470c(RD1_0), .Read_Data_2_12_0_772128e8(RD2_0));
  L_4x13_SRAM l_4x13_sram_2 (
    .Write_Data_12_0_6c18a168(Write_Data_12_0_6c18a168), .Write_Enable_46f62da9(W1),
    .Write_Address_1_0_5750fd8a(Write_Address_3_0_fc297a62[1:0]),
    .Read_Address_1_1_0_b69a7a8d(Read_Address_1_3_0_3886bda4[1:0]), .Read_Address2_Enable_1a2e55ec(R2_1),
    .Read_Address_2_1_0_ce9bad49(Read_Address_2_3_0_9b81066c[1:0]), .Clock(Clock),
    .Read_Address1_Enable_996bc5a8(R1_1), .Read_Data_1_12_0_a238470c(RD1_1), .Read_Data_2_12_0_772128e8(RD2_1));
  L_4x13_SRAM l_4x13_sram_3 (
    .Write_Data_12_0_6c18a168(Write_Data_12_0_6c18a168), .Write_Enable_46f62da9(W2),
    .Write_Address_1_0_5750fd8a(Write_Address_3_0_fc297a62[1:0]),
    .Read_Address_1_1_0_b69a7a8d(Read_Address_1_3_0_3886bda4[1:0]), .Read_Address2_Enable_1a2e55ec(R2_2),
    .Read_Address_2_1_0_ce9bad49(Read_Address_2_3_0_9b81066c[1:0]), .Clock(Clock),
    .Read_Address1_Enable_996bc5a8(R1_2), .Read_Data_1_12_0_a238470c(RD1_2), .Read_Data_2_12_0_772128e8(RD2_2));
  L_4x13_SRAM l_4x13_sram_4 (
    .Write_Data_12_0_6c18a168(Write_Data_12_0_6c18a168), .Write_Enable_46f62da9(W3),
    .Write_Address_1_0_5750fd8a(Write_Address_3_0_fc297a62[1:0]),
    .Read_Address_1_1_0_b69a7a8d(Read_Address_1_3_0_3886bda4[1:0]), .Read_Address2_Enable_1a2e55ec(R2_3),
    .Read_Address_2_1_0_ce9bad49(Read_Address_2_3_0_9b81066c[1:0]), .Clock(Clock),
    .Read_Address1_Enable_996bc5a8(R1_3), .Read_Data_1_12_0_a238470c(RD1_3), .Read_Data_2_12_0_772128e8(RD2_3));
  assign Read_Data_1_12_0_a238470c = RD1_0 | RD1_1 | RD1_2 | RD1_3;  // OR_Gate or_1, 13 bits wide
  assign Read_Data_2_12_0_772128e8 = RD2_0 | RD2_1 | RD2_2 | RD2_3;  // OR_Gate or_2, 13 bits wide

  // Other names for the same wires on the sheet: RA1_E = Read_Address1_Enable_996bc5a8;
  //   RA2_E = Read_Address2_Enable_1a2e55ec; RA1_0[1:0] = Read_Address_1_3_0_3886bda4[1:0];
  //   RA1_1[1:0] = Read_Address_1_3_0_3886bda4[3:2]; RA2_0[1:0] = Read_Address_2_3_0_9b81066c[1:0];
  //   RA2_1[1:0] = Read_Address_2_3_0_9b81066c[3:2]; WD[12:0] = Write_Data_12_0_6c18a168; WE = Write_Enable_46f62da9;
  //   WA0[1:0] = Write_Address_3_0_fc297a62[1:0]; WA1[1:0] = Write_Address_3_0_fc297a62[3:2]
endmodule

module L_64x13_SRAM (
  input  [5:0] Read_Address_1_5_0_e2f34ef3,
  input  [5:0] Read_Address_2_5_0_c5beac2e,
  input  Read_Address1_Enable_996bc5a8,
  input  Read_Address2_Enable_1a2e55ec,
  input  [5:0] Write_Address_5_0_b2a42571,
  input  [12:0] Write_Data_12_0_6c18a168,
  input  Write_Enable_46f62da9,
  input  Clock,
  output [12:0] Read_Data_1_12_0_a238470c,
  output [12:0] Read_Data_2_12_0_772128e8
);

  wire R1_0, R1_1, R1_2, R1_3, R2_0, R2_1, R2_2, R2_3, W0, W1, W2, W3;
  wire [12:0] RD1_0, RD1_1, RD1_2, RD1_3, RD2_0, RD2_1, RD2_2, RD2_3;

  Decoder #(.select(2)) decoder_1 (
    .out0(R1_0), .out1(R1_1), .out2(R1_2), .out3(R1_3), .sel(Read_Address_1_5_0_e2f34ef3[5:4]),
    .en(Read_Address1_Enable_996bc5a8));
  Decoder #(.select(2)) decoder_2 (
    .out0(R2_0), .out1(R2_1), .out2(R2_2), .out3(R2_3), .sel(Read_Address_2_5_0_c5beac2e[5:4]),
    .en(Read_Address2_Enable_1a2e55ec));
  Decoder #(.select(2)) decoder_3 (
    .out0(W0), .out1(W1), .out2(W2), .out3(W3), .sel(Write_Address_5_0_b2a42571[5:4]),
    .en(Write_Enable_46f62da9));
  L_16x13_SRAM l_16x13_sram_1 (
    .Clock(Clock), .Write_Enable_46f62da9(W0), .Write_Address_3_0_fc297a62(Write_Address_5_0_b2a42571[3:0]),
    .Read_Address_1_3_0_3886bda4(Read_Address_1_5_0_e2f34ef3[3:0]),
    .Read_Address_2_3_0_9b81066c(Read_Address_2_5_0_c5beac2e[3:0]), .Read_Address1_Enable_996bc5a8(R1_0),
    .Read_Address2_Enable_1a2e55ec(R2_0), .Write_Data_12_0_6c18a168(Write_Data_12_0_6c18a168),
    .Read_Data_1_12_0_a238470c(RD1_0), .Read_Data_2_12_0_772128e8(RD2_0));
  L_16x13_SRAM l_16x13_sram_2 (
    .Clock(Clock), .Write_Enable_46f62da9(W1), .Write_Address_3_0_fc297a62(Write_Address_5_0_b2a42571[3:0]),
    .Read_Address_1_3_0_3886bda4(Read_Address_1_5_0_e2f34ef3[3:0]),
    .Read_Address_2_3_0_9b81066c(Read_Address_2_5_0_c5beac2e[3:0]), .Read_Address1_Enable_996bc5a8(R1_1),
    .Read_Address2_Enable_1a2e55ec(R2_1), .Write_Data_12_0_6c18a168(Write_Data_12_0_6c18a168),
    .Read_Data_1_12_0_a238470c(RD1_1), .Read_Data_2_12_0_772128e8(RD2_1));
  L_16x13_SRAM l_16x13_sram_3 (
    .Clock(Clock), .Write_Enable_46f62da9(W2), .Write_Address_3_0_fc297a62(Write_Address_5_0_b2a42571[3:0]),
    .Read_Address_1_3_0_3886bda4(Read_Address_1_5_0_e2f34ef3[3:0]),
    .Read_Address_2_3_0_9b81066c(Read_Address_2_5_0_c5beac2e[3:0]), .Read_Address1_Enable_996bc5a8(R1_2),
    .Read_Address2_Enable_1a2e55ec(R2_2), .Write_Data_12_0_6c18a168(Write_Data_12_0_6c18a168),
    .Read_Data_1_12_0_a238470c(RD1_2), .Read_Data_2_12_0_772128e8(RD2_2));
  L_16x13_SRAM l_16x13_sram_4 (
    .Clock(Clock), .Write_Enable_46f62da9(W3), .Write_Address_3_0_fc297a62(Write_Address_5_0_b2a42571[3:0]),
    .Read_Address_1_3_0_3886bda4(Read_Address_1_5_0_e2f34ef3[3:0]),
    .Read_Address_2_3_0_9b81066c(Read_Address_2_5_0_c5beac2e[3:0]), .Read_Address1_Enable_996bc5a8(R1_3),
    .Read_Address2_Enable_1a2e55ec(R2_3), .Write_Data_12_0_6c18a168(Write_Data_12_0_6c18a168),
    .Read_Data_1_12_0_a238470c(RD1_3), .Read_Data_2_12_0_772128e8(RD2_3));
  assign Read_Data_1_12_0_a238470c = RD1_0 | RD1_1 | RD1_2 | RD1_3;  // OR_Gate or_1, 13 bits wide
  assign Read_Data_2_12_0_772128e8 = RD2_0 | RD2_1 | RD2_2 | RD2_3;  // OR_Gate or_2, 13 bits wide

  // Other names for the same wires on the sheet: RA1_E = Read_Address1_Enable_996bc5a8;
  //   RA2_E = Read_Address2_Enable_1a2e55ec; RA1_0[3:0] = Read_Address_1_5_0_e2f34ef3[3:0];
  //   RA1_1[1:0] = Read_Address_1_5_0_e2f34ef3[5:4]; RA2_0[3:0] = Read_Address_2_5_0_c5beac2e[3:0];
  //   RA2_1[1:0] = Read_Address_2_5_0_c5beac2e[5:4]; WD[12:0] = Write_Data_12_0_6c18a168; WE = Write_Enable_46f62da9;
  //   WA0[3:0] = Write_Address_5_0_b2a42571[3:0]; WA1[1:0] = Write_Address_5_0_b2a42571[5:4]
endmodule

module L_128X13_SRAM (
  input  [6:0] Read_Address_1_6_0_de8e8647,
  input  [6:0] Read_Address_2_6_0_838d20dd,
  input  [6:0] Write_Address_6_0_da5045b5,
  input  [12:0] Write_Data_12_0_6c18a168,
  input  Write_Enable_46f62da9,
  input  Clock,
  output [12:0] Read_Data_1_12_0_a238470c,
  output [12:0] Read_Data_2_12_0_772128e8
);

  wire R1_0, R1_1, R2_0, R2_1, W0, W1;
  wire [12:0] RD1_0, RD1_1, RD2_0, RD2_1;

  Decoder #(.enable("false")) decoder_1 (.out0(R1_0), .out1(R1_1), .sel(Read_Address_1_6_0_de8e8647[6]));
  Decoder #(.enable("false")) decoder_2 (.out0(R2_0), .out1(R2_1), .sel(Read_Address_2_6_0_838d20dd[6]));
  Decoder decoder_3 (.out0(W0), .out1(W1), .sel(Write_Address_6_0_da5045b5[6]), .en(Write_Enable_46f62da9));
  L_64x13_SRAM l_64x13_sram_1 (
    .Clock(Clock), .Write_Enable_46f62da9(W0),
    .Read_Address_1_5_0_e2f34ef3(Read_Address_1_6_0_de8e8647[5:0]),
    .Read_Address_2_5_0_c5beac2e(Read_Address_2_6_0_838d20dd[5:0]),
    .Write_Address_5_0_b2a42571(Write_Address_6_0_da5045b5[5:0]), .Read_Address1_Enable_996bc5a8(R1_0),
    .Read_Address2_Enable_1a2e55ec(R2_0), .Write_Data_12_0_6c18a168(Write_Data_12_0_6c18a168),
    .Read_Data_1_12_0_a238470c(RD1_0), .Read_Data_2_12_0_772128e8(RD2_0));
  L_64x13_SRAM l_64x13_sram_2 (
    .Clock(Clock), .Write_Enable_46f62da9(W1),
    .Read_Address_1_5_0_e2f34ef3(Read_Address_1_6_0_de8e8647[5:0]),
    .Read_Address_2_5_0_c5beac2e(Read_Address_2_6_0_838d20dd[5:0]),
    .Write_Address_5_0_b2a42571(Write_Address_6_0_da5045b5[5:0]), .Read_Address1_Enable_996bc5a8(R1_1),
    .Read_Address2_Enable_1a2e55ec(R2_1), .Write_Data_12_0_6c18a168(Write_Data_12_0_6c18a168),
    .Read_Data_1_12_0_a238470c(RD1_1), .Read_Data_2_12_0_772128e8(RD2_1));
  assign Read_Data_1_12_0_a238470c = RD1_0 | RD1_1;  // OR_Gate or_1, 13 bits wide
  assign Read_Data_2_12_0_772128e8 = RD2_0 | RD2_1;  // OR_Gate or_2, 13 bits wide

  // Other names for the same wires on the sheet: RA1_0[5:0] = Read_Address_1_6_0_de8e8647[5:0];
  //   RA1_1 = Read_Address_1_6_0_de8e8647[6]; RA2_0[5:0] = Read_Address_2_6_0_838d20dd[5:0];
  //   RA2_1 = Read_Address_2_6_0_838d20dd[6]; WD[12:0] = Write_Data_12_0_6c18a168; WE = Write_Enable_46f62da9;
  //   WA0[5:0] = Write_Address_6_0_da5045b5[5:0]; WA1 = Write_Address_6_0_da5045b5[6]
endmodule

module RAM_Testing (
  input  [6:0] Read_Address_1_6_0_de8e8647,
  input  [6:0] Read_Address_2_6_0_838d20dd,
  input  [6:0] Write_Address_6_0_da5045b5,
  input  [12:0] Write_Data_12_0_6c18a168,
  input  Write_Enable_46f62da9,
  input  Clock,
  output [12:0] Read_Data_1_12_0_a238470c,
  output [12:0] Read_Data_2_12_0_772128e8
);

  L_128X13_SRAM l_128x13_sram_1 (
    .Clock(Clock), .Write_Enable_46f62da9(Write_Enable_46f62da9),
    .Write_Address_6_0_da5045b5(Write_Address_6_0_da5045b5),
    .Read_Address_1_6_0_de8e8647(Read_Address_1_6_0_de8e8647),
    .Read_Address_2_6_0_838d20dd(Read_Address_2_6_0_838d20dd),
    .Write_Data_12_0_6c18a168(Write_Data_12_0_6c18a168),
    .Read_Data_1_12_0_a238470c(Read_Data_1_12_0_a238470c),
    .Read_Data_2_12_0_772128e8(Read_Data_2_12_0_772128e8));
endmodule
