// Logisim project Unsigned_Divider.circ as structural Verilog: 4 circuits, main circuit FS
module FS (
  input  A,
  input  B,
  input  Bin,
  output D,
  output Bout
);

  wire and_1_out, and_2_out, and_3_out, not_1_out, not_2_out, or_1_out, xor_1_out;

  xor xor_1 (xor_1_out, A, B);
  not not_1 (not_1_out, A);
  and and_1 (and_1_out, not_1_out, Bin);
  not not_2 (not_2_out, A);
  and and_2 (and_2_out, not_2_out, B);
  xor xor_2 (D, xor_1_out, Bin);
  or or_1 (or_1_out, and_1_out, and_2_out);
  and and_3 (and_3_out, B, Bin);
  or or_2 (Bout, or_1_out, and_3_out);
endmodule

module Cell_D_65ffe174 (
  input  A,
  input  B,
  input  Bin,
  input  Sel,
  output Bout,
  output Sel_copy,
  output A_D_c81a9392,
  output B_copy
);

  wire fs_1_d;

  FS fs_1 (.A(A), .B(B), .Bin(Bin), .D(fs_1_d), .Bout(Bout));
  Multiplexer multiplexer_1 (.in0(fs_1_d), .in1(A), .out(A_D_c81a9392), .sel(Sel));

  assign B_copy = B;
  assign Sel_copy = Sel;
endmodule

// A0
module L_2_bit_Unsigned_Divider_5e81c541 (
  input  A1,
  input  A0,
  input  B1,
  input  B0,
  output Q1,
  output Q0,
  output R1,
  output R0,
  output Exception
);

  wire cell_d_65ffe174_1_b_copy, cell_d_65ffe174_1_bout, cell_d_65ffe174_1_sel_copy,
       cell_d_65ffe174_2_a_d_c81a9392, cell_d_65ffe174_2_b_copy, cell_d_65ffe174_2_bout,
       cell_d_65ffe174_3_bout, cell_d_65ffe174_3_sel_copy, cell_d_65ffe174_4_bout;

  not not_1 (Q1, cell_d_65ffe174_1_bout);
  not not_2 (Q0, cell_d_65ffe174_3_bout);
  Cell_D_65ffe174 cell_d_65ffe174_1 (
    .Sel(cell_d_65ffe174_1_bout), .A(1'b0), .B(B1), .Bin(cell_d_65ffe174_2_bout),
    .Bout(cell_d_65ffe174_1_bout), .Sel_copy(cell_d_65ffe174_1_sel_copy), .B_copy(cell_d_65ffe174_1_b_copy));  // open: A_D_c81a9392
  Cell_D_65ffe174 cell_d_65ffe174_2 (
    .Sel(cell_d_65ffe174_1_sel_copy), .A(A1), .B(B0), .Bin(1'b0), .Bout(cell_d_65ffe174_2_bout),
    .A_D_c81a9392(cell_d_65ffe174_2_a_d_c81a9392), .B_copy(cell_d_65ffe174_2_b_copy));  // open: Sel_copy
  Cell_D_65ffe174 cell_d_65ffe174_3 (
    .Sel(cell_d_65ffe174_3_bout), .A(cell_d_65ffe174_2_a_d_c81a9392), .B(cell_d_65ffe174_1_b_copy),
    .Bin(cell_d_65ffe174_4_bout), .Bout(cell_d_65ffe174_3_bout), .A_D_c81a9392(R1),
    .Sel_copy(cell_d_65ffe174_3_sel_copy));  // open: B_copy
  Cell_D_65ffe174 cell_d_65ffe174_4 (
    .Sel(cell_d_65ffe174_3_sel_copy), .A(A0), .B(cell_d_65ffe174_2_b_copy), .Bin(1'b0),
    .Bout(cell_d_65ffe174_4_bout), .A_D_c81a9392(R0));  // open: Sel_copy, B_copy
  nor nor_1 (Exception, B1, B0);
endmodule

module L_4_bit_Unsigned_Divider_a4ae8a96 (
  input  A3,
  input  A2,
  input  A1,
  input  A0,
  input  B3,
  input  B2,
  input  B1,
  input  B0,
  output Q3,
  output Q2,
  output Q1,
  output Q0,
  output R3,
  output R2,
  output R1,
  output R0,
  output Exception
);

  wire cell_d_65ffe174_1_b_copy, cell_d_65ffe174_1_bout, cell_d_65ffe174_1_sel_copy,
       cell_d_65ffe174_2_a_d_c81a9392, cell_d_65ffe174_2_b_copy, cell_d_65ffe174_2_bout,
       cell_d_65ffe174_2_sel_copy, cell_d_65ffe174_3_b_copy, cell_d_65ffe174_3_bout,
       cell_d_65ffe174_3_sel_copy, cell_d_65ffe174_4_a_d_c81a9392, cell_d_65ffe174_4_b_copy,
       cell_d_65ffe174_4_bout, cell_d_65ffe174_4_sel_copy, cell_d_65ffe174_5_a_d_c81a9392,
       cell_d_65ffe174_5_b_copy, cell_d_65ffe174_5_bout, cell_d_65ffe174_5_sel_copy,
       cell_d_65ffe174_6_b_copy, cell_d_65ffe174_6_bout, cell_d_65ffe174_6_sel_copy,
       cell_d_65ffe174_7_a_d_c81a9392, cell_d_65ffe174_7_b_copy, cell_d_65ffe174_7_bout,
       cell_d_65ffe174_8_a_d_c81a9392, cell_d_65ffe174_8_b_copy, cell_d_65ffe174_8_bout,
       cell_d_65ffe174_8_sel_copy, cell_d_65ffe174_9_a_d_c81a9392, cell_d_65ffe174_9_b_copy,
       cell_d_65ffe174_9_bout, cell_d_65ffe174_9_sel_copy, cell_d_65ffe174_10_bout,
       cell_d_65ffe174_10_sel_copy, cell_d_65ffe174_11_a_d_c81a9392, cell_d_65ffe174_11_b_copy,
       cell_d_65ffe174_11_bout, cell_d_65ffe174_12_a_d_c81a9392, cell_d_65ffe174_12_b_copy,
       cell_d_65ffe174_12_bout, cell_d_65ffe174_12_sel_copy, cell_d_65ffe174_13_bout,
       cell_d_65ffe174_13_sel_copy, cell_d_65ffe174_14_a_d_c81a9392, cell_d_65ffe174_14_b_copy,
       cell_d_65ffe174_14_bout, cell_d_65ffe174_15_bout, cell_d_65ffe174_15_sel_copy, cell_d_65ffe174_16_bout;

  not not_1 (Q3, cell_d_65ffe174_1_bout);
  Cell_D_65ffe174 cell_d_65ffe174_1 (
    .Sel(cell_d_65ffe174_1_bout), .A(1'b0), .B(B3), .Bin(cell_d_65ffe174_2_bout),
    .Bout(cell_d_65ffe174_1_bout), .Sel_copy(cell_d_65ffe174_1_sel_copy), .B_copy(cell_d_65ffe174_1_b_copy));  // open: A_D_c81a9392
  not not_2 (Q2, cell_d_65ffe174_3_bout);
  Cell_D_65ffe174 cell_d_65ffe174_2 (
    .Sel(cell_d_65ffe174_1_sel_copy), .A(1'b0), .B(B2), .Bin(cell_d_65ffe174_4_bout),
    .Bout(cell_d_65ffe174_2_bout), .A_D_c81a9392(cell_d_65ffe174_2_a_d_c81a9392),
    .Sel_copy(cell_d_65ffe174_2_sel_copy), .B_copy(cell_d_65ffe174_2_b_copy));
  Cell_D_65ffe174 cell_d_65ffe174_3 (
    .Sel(cell_d_65ffe174_3_bout), .A(cell_d_65ffe174_2_a_d_c81a9392), .B(cell_d_65ffe174_1_b_copy),
    .Bin(cell_d_65ffe174_5_bout), .Bout(cell_d_65ffe174_3_bout), .Sel_copy(cell_d_65ffe174_3_sel_copy),
    .B_copy(cell_d_65ffe174_3_b_copy));  // open: A_D_c81a9392
  not not_3 (Q1, cell_d_65ffe174_6_bout);
  not not_4 (Q0, cell_d_65ffe174_10_bout);
  Cell_D_65ffe174 cell_d_65ffe174_4 (
    .Sel(cell_d_65ffe174_2_sel_copy), .A(1'b0), .B(B1), .Bin(cell_d_65ffe174_7_bout),
    .Bout(cell_d_65ffe174_4_bout), .A_D_c81a9392(cell_d_65ffe174_4_a_d_c81a9392),
    .Sel_copy(cell_d_65ffe174_4_sel_copy), .B_copy(cell_d_65ffe174_4_b_copy));
  Cell_D_65ffe174 cell_d_65ffe174_5 (
    .Sel(cell_d_65ffe174_3_sel_copy), .A(cell_d_65ffe174_4_a_d_c81a9392), .B(cell_d_65ffe174_2_b_copy),
    .Bin(cell_d_65ffe174_8_bout), .Bout(cell_d_65ffe174_5_bout),
    .A_D_c81a9392(cell_d_65ffe174_5_a_d_c81a9392), .Sel_copy(cell_d_65ffe174_5_sel_copy),
    .B_copy(cell_d_65ffe174_5_b_copy));
  Cell_D_65ffe174 cell_d_65ffe174_6 (
    .Sel(cell_d_65ffe174_6_bout), .A(cell_d_65ffe174_5_a_d_c81a9392), .B(cell_d_65ffe174_3_b_copy),
    .Bin(cell_d_65ffe174_9_bout), .Bout(cell_d_65ffe174_6_bout), .Sel_copy(cell_d_65ffe174_6_sel_copy),
    .B_copy(cell_d_65ffe174_6_b_copy));  // open: A_D_c81a9392
  Cell_D_65ffe174 cell_d_65ffe174_7 (
    .Sel(cell_d_65ffe174_4_sel_copy), .A(A3), .B(B0), .Bin(1'b0), .Bout(cell_d_65ffe174_7_bout),
    .A_D_c81a9392(cell_d_65ffe174_7_a_d_c81a9392), .B_copy(cell_d_65ffe174_7_b_copy));  // open: Sel_copy
  Cell_D_65ffe174 cell_d_65ffe174_8 (
    .Sel(cell_d_65ffe174_5_sel_copy), .A(cell_d_65ffe174_7_a_d_c81a9392), .B(cell_d_65ffe174_4_b_copy),
    .Bin(cell_d_65ffe174_11_bout), .Bout(cell_d_65ffe174_8_bout),
    .A_D_c81a9392(cell_d_65ffe174_8_a_d_c81a9392), .Sel_copy(cell_d_65ffe174_8_sel_copy),
    .B_copy(cell_d_65ffe174_8_b_copy));
  Cell_D_65ffe174 cell_d_65ffe174_9 (
    .Sel(cell_d_65ffe174_6_sel_copy), .A(cell_d_65ffe174_8_a_d_c81a9392), .B(cell_d_65ffe174_5_b_copy),
    .Bin(cell_d_65ffe174_12_bout), .Bout(cell_d_65ffe174_9_bout),
    .A_D_c81a9392(cell_d_65ffe174_9_a_d_c81a9392), .Sel_copy(cell_d_65ffe174_9_sel_copy),
    .B_copy(cell_d_65ffe174_9_b_copy));
  Cell_D_65ffe174 cell_d_65ffe174_10 (
    .Sel(cell_d_65ffe174_10_bout), .A(cell_d_65ffe174_9_a_d_c81a9392), .B(cell_d_65ffe174_6_b_copy),
    .Bin(cell_d_65ffe174_13_bout), .Bout(cell_d_65ffe174_10_bout), .A_D_c81a9392(R3),
    .Sel_copy(cell_d_65ffe174_10_sel_copy));  // open: B_copy
  Cell_D_65ffe174 cell_d_65ffe174_11 (
    .Sel(cell_d_65ffe174_8_sel_copy), .A(A2), .B(cell_d_65ffe174_7_b_copy), .Bin(1'b0),
    .Bout(cell_d_65ffe174_11_bout), .A_D_c81a9392(cell_d_65ffe174_11_a_d_c81a9392),
    .B_copy(cell_d_65ffe174_11_b_copy));  // open: Sel_copy
  Cell_D_65ffe174 cell_d_65ffe174_12 (
    .Sel(cell_d_65ffe174_9_sel_copy), .A(cell_d_65ffe174_11_a_d_c81a9392), .B(cell_d_65ffe174_8_b_copy),
    .Bin(cell_d_65ffe174_14_bout), .Bout(cell_d_65ffe174_12_bout),
    .A_D_c81a9392(cell_d_65ffe174_12_a_d_c81a9392), .Sel_copy(cell_d_65ffe174_12_sel_copy),
    .B_copy(cell_d_65ffe174_12_b_copy));
  Cell_D_65ffe174 cell_d_65ffe174_13 (
    .Sel(cell_d_65ffe174_10_sel_copy), .A(cell_d_65ffe174_12_a_d_c81a9392), .B(cell_d_65ffe174_9_b_copy),
    .Bin(cell_d_65ffe174_15_bout), .Bout(cell_d_65ffe174_13_bout), .A_D_c81a9392(R2),
    .Sel_copy(cell_d_65ffe174_13_sel_copy));  // open: B_copy
  Cell_D_65ffe174 cell_d_65ffe174_14 (
    .Sel(cell_d_65ffe174_12_sel_copy), .A(A1), .B(cell_d_65ffe174_11_b_copy), .Bin(1'b0),
    .Bout(cell_d_65ffe174_14_bout), .A_D_c81a9392(cell_d_65ffe174_14_a_d_c81a9392),
    .B_copy(cell_d_65ffe174_14_b_copy));  // open: Sel_copy
  Cell_D_65ffe174 cell_d_65ffe174_15 (
    .Sel(cell_d_65ffe174_13_sel_copy), .A(cell_d_65ffe174_14_a_d_c81a9392), .B(cell_d_65ffe174_12_b_copy),
    .Bin(cell_d_65ffe174_16_bout), .Bout(cell_d_65ffe174_15_bout), .A_D_c81a9392(R1),
    .Sel_copy(cell_d_65ffe174_15_sel_copy));  // open: B_copy
  Cell_D_65ffe174 cell_d_65ffe174_16 (
    .Sel(cell_d_65ffe174_15_sel_copy), .A(A0), .B(cell_d_65ffe174_14_b_copy), .Bin(1'b0),
    .Bout(cell_d_65ffe174_16_bout), .A_D_c81a9392(R0));  // open: Sel_copy, B_copy
  nor nor_1 (Exception, B3, B2, B1, B0);
endmodule
