// Logisim project Unsigned_Multiplier_Library.circ as structural Verilog: 4 circuits, main circuit FA
module FA (
  input  a,
  input  b,
  input  Cin,
  output S,
  output Cout
);

  wire and_1_out, and_2_out, xor_1_out;

  xor xor_1 (xor_1_out, a, b);
  xor xor_2 (S, xor_1_out, Cin);
  and and_1 (and_1_out, Cin, xor_1_out);
  and and_2 (and_2_out, a, b);
  or or_1 (Cout, and_1_out, and_2_out);
endmodule

module Cell_M (
  input  x,
  input  y,
  input  b,
  input  Cin,
  output Cout,
  output x_copy,
  output s
);

  wire and_1_out;

  and and_1 (and_1_out, x, y);
  FA fa_1 (.a(and_1_out), .b(b), .Cin(Cin), .S(s), .Cout(Cout));

  assign x_copy = x;
endmodule

module Two_into_Two_MUL (
  input  X1,
  input  X0,
  input  Y0,
  input  Y1,
  output P3,
  output P2,
  output P1,
  output P0
);

  wire cell_m_2_cout, cell_m_2_s, cell_m_2_x_copy, cell_m_3_cout, cell_m_4_cout, cell_m_4_x_copy;

  Cell_M cell_m_1 (
    .x(cell_m_2_x_copy), .y(Y1), .b(cell_m_2_cout), .Cin(cell_m_3_cout), .Cout(P3), .s(P2));  // open: x_copy
  Cell_M cell_m_2 (
    .x(X1), .y(Y0), .b(1'b0), .Cin(cell_m_4_cout), .Cout(cell_m_2_cout), .x_copy(cell_m_2_x_copy),
    .s(cell_m_2_s));
  Cell_M cell_m_3 (
    .x(cell_m_4_x_copy), .y(Y1), .b(cell_m_2_s), .Cin(1'b0), .Cout(cell_m_3_cout), .s(P1));  // open: x_copy
  Cell_M cell_m_4 (.x(X0), .y(Y0), .b(1'b0), .Cin(1'b0), .Cout(cell_m_4_cout), .x_copy(cell_m_4_x_copy), .s(P0));
endmodule

module Four_into_Four_MUL (
  input  X3,
  input  X2,
  input  X1,
  input  X0,
  input  Y0,
  input  Y1,
  input  Y2,
  input  Y3,
  output P7,
  output P6,
  output P5,
  output P4,
  output P3,
  output P2,
  output P1,
  output P0
);

  wire cell_m_2_cout, cell_m_2_s, cell_m_2_x_copy, cell_m_3_cout, cell_m_4_cout, cell_m_4_s, cell_m_4_x_copy,
       cell_m_5_cout, cell_m_5_s, cell_m_5_x_copy, cell_m_6_cout, cell_m_7_cout, cell_m_7_s, cell_m_7_x_copy,
       cell_m_8_cout, cell_m_8_s, cell_m_8_x_copy, cell_m_9_cout, cell_m_9_s, cell_m_9_x_copy,
       cell_m_10_cout, cell_m_11_cout, cell_m_11_s, cell_m_11_x_copy, cell_m_12_cout, cell_m_12_s,
       cell_m_12_x_copy, cell_m_13_cout, cell_m_13_x_copy, cell_m_14_cout, cell_m_14_s, cell_m_14_x_copy,
       cell_m_15_cout, cell_m_15_x_copy, cell_m_16_cout, cell_m_16_x_copy;

  Cell_M cell_m_1 (
    .x(cell_m_2_x_copy), .y(Y3), .b(cell_m_2_cout), .Cin(cell_m_3_cout), .Cout(P7), .s(P6));  // open: x_copy
  Cell_M cell_m_2 (
    .x(cell_m_4_x_copy), .y(Y2), .b(cell_m_4_cout), .Cin(cell_m_5_cout), .Cout(cell_m_2_cout),
    .x_copy(cell_m_2_x_copy), .s(cell_m_2_s));
  Cell_M cell_m_3 (
    .x(cell_m_5_x_copy), .y(Y3), .b(cell_m_2_s), .Cin(cell_m_6_cout), .Cout(cell_m_3_cout), .s(P5));  // open: x_copy
  Cell_M cell_m_4 (
    .x(cell_m_7_x_copy), .y(Y1), .b(cell_m_7_cout), .Cin(cell_m_8_cout), .Cout(cell_m_4_cout),
    .x_copy(cell_m_4_x_copy), .s(cell_m_4_s));
  Cell_M cell_m_5 (
    .x(cell_m_8_x_copy), .y(Y2), .b(cell_m_4_s), .Cin(cell_m_9_cout), .Cout(cell_m_5_cout),
    .x_copy(cell_m_5_x_copy), .s(cell_m_5_s));
  Cell_M cell_m_6 (
    .x(cell_m_9_x_copy), .y(Y3), .b(cell_m_5_s), .Cin(cell_m_10_cout), .Cout(cell_m_6_cout), .s(P4));  // open: x_copy
  Cell_M cell_m_7 (
    .x(X3), .y(Y0), .b(1'b0), .Cin(cell_m_11_cout), .Cout(cell_m_7_cout), .x_copy(cell_m_7_x_copy),
    .s(cell_m_7_s));
  Cell_M cell_m_8 (
    .x(cell_m_11_x_copy), .y(Y1), .b(cell_m_7_s), .Cin(cell_m_12_cout), .Cout(cell_m_8_cout),
    .x_copy(cell_m_8_x_copy), .s(cell_m_8_s));
  Cell_M cell_m_9 (
    .x(cell_m_12_x_copy), .y(Y2), .b(cell_m_8_s), .Cin(cell_m_13_cout), .Cout(cell_m_9_cout),
    .x_copy(cell_m_9_x_copy), .s(cell_m_9_s));
  Cell_M cell_m_10 (
    .x(cell_m_13_x_copy), .y(Y3), .b(cell_m_9_s), .Cin(1'b0), .Cout(cell_m_10_cout), .s(P3));  // open: x_copy
  Cell_M cell_m_11 (
    .x(X2), .y(Y0), .b(1'b0), .Cin(cell_m_14_cout), .Cout(cell_m_11_cout), .x_copy(cell_m_11_x_copy),
    .s(cell_m_11_s));
  Cell_M cell_m_12 (
    .x(cell_m_14_x_copy), .y(Y1), .b(cell_m_11_s), .Cin(cell_m_15_cout), .Cout(cell_m_12_cout),
    .x_copy(cell_m_12_x_copy), .s(cell_m_12_s));
  Cell_M cell_m_13 (
    .x(cell_m_15_x_copy), .y(Y2), .b(cell_m_12_s), .Cin(1'b0), .Cout(cell_m_13_cout),
    .x_copy(cell_m_13_x_copy), .s(P2));
  Cell_M cell_m_14 (
    .x(X1), .y(Y0), .b(1'b0), .Cin(cell_m_16_cout), .Cout(cell_m_14_cout), .x_copy(cell_m_14_x_copy),
    .s(cell_m_14_s));
  Cell_M cell_m_15 (
    .x(cell_m_16_x_copy), .y(Y1), .b(cell_m_14_s), .Cin(1'b0), .Cout(cell_m_15_cout),
    .x_copy(cell_m_15_x_copy), .s(P1));
  Cell_M cell_m_16 (.x(X0), .y(Y0), .b(1'b0), .Cin(1'b0), .Cout(cell_m_16_cout), .x_copy(cell_m_16_x_copy), .s(P0));
endmodule
