// Logisim project alu1bit.circ as structural Verilog: 11 circuits, main circuit and1bit
module and1bit (
  input  A,
  input  B,
  output R
);

  and and_1 (R, A, B);
endmodule

module or1bit (
  input  A,
  input  B,
  output R
);

  or or_1 (R, A, B);
endmodule

module xor1bit (
  input  A,
  input  B,
  output R
);

  nor nor_1 (R, A, B);
endmodule

module leftshift1bit (
  input  A,
  input  l_shift,
  output R
);

  Multiplexer multiplexer_1 (.in0(A), .in1(1'b0), .out(R), .sel(l_shift));
endmodule

module rightshift1bit (
  input  A,
  input  r_shift,
  output R
);

  Multiplexer multiplexer_1 (.in0(A), .in1(1'b0), .out(R), .sel(r_shift));
endmodule

module fulladder1bit (
  input  A,
  input  B,
  input  Ci,
  output S,
  output Co
);

  wire and_1_out, and_2_out, xor_1_out;

  and and_1 (and_1_out, A, B);
  xor xor_1 (xor_1_out, A, B);
  and and_2 (and_2_out, xor_1_out, Ci);
  xor xor_2 (S, xor_1_out, Ci);
  or or_1 (Co, and_2_out, and_1_out);
endmodule

module addsub1bit (
  input  A,
  input  B,
  input  Add_Sub_sel,
  output Co,
  output S
);

  wire xor_1_out;

  xor xor_1 (xor_1_out, Add_Sub_sel, B);
  fulladder1bit fulladder1bit_1 (.A(A), .B(xor_1_out), .Ci(Add_Sub_sel), .S(S), .Co(Co));
endmodule

module leftrotate1bit (
  input  A,
  input  L_rotate,
  output R
);

  Multiplexer multiplexer_1 (.in0(A), .in1(A), .out(R), .sel(L_rotate));
endmodule

module rightrotate1bit (
  input  A,
  input  R_rotate,
  output R
);

  Multiplexer multiplexer_1 (.in0(A), .in1(A), .out(R), .sel(R_rotate));
endmodule

module not1bit (
  input  A,
  output R
);

  not not_1 (R, A);
endmodule

module alu1bit (
  input  A,
  input  B,
  input  [3:0] Sel,
  output out_4
);

  wire ANDr, Left_rotate, Left_shift, NOTr, Orr, Right_rotate, Right_shift, Sum_Sub, undriven, Xorr;

  and1bit and1bit_1 (.A(A), .B(B), .R(ANDr));
  or1bit or1bit_1 (.A(A), .B(B), .R(Orr));
  xor1bit xor1bit_1 (.A(A), .B(B), .R(Xorr));
  leftshift1bit leftshift1bit_1 (.A(A), .l_shift(B), .R(Left_shift));
  rightshift1bit rightshift1bit_1 (.A(A), .r_shift(B), .R(Right_shift));
  addsub1bit addsub1bit_1 (.B(B), .Add_Sub_sel(Sel[1]), .A(A), .S(Sum_Sub));  // open: Co
  leftrotate1bit leftrotate1bit_1 (.A(A), .L_rotate(B), .R(Left_rotate));
  rightrotate1bit rightrotate1bit_1 (.A(A), .R_rotate(B), .R(Right_rotate));
  not1bit not1bit_1 (.A(A), .R(NOTr));
  Multiplexer #(.select(4)) multiplexer_1 (
    .in0(ANDr), .in1(Orr), .in2(Xorr), .in3(Left_shift), .in4(Right_shift), .in5(Sum_Sub), .in6(Sum_Sub),
    .in7(undriven), .in8(Left_rotate), .in9(Right_rotate), .in10(NOTr), .out(out_4), .sel(Sel));  // open: in11, in12, in13, in14, in15

  // Other names for the same wires on the sheet: Add_Sub_sel = Sel[1]
endmodule
