// Logisim project alu2bit.circ as structural Verilog: 11 circuits, main circuit and2bit
module and2bit (
  input  [1:0] A,
  input  [1:0] B,
  output [1:0] R
);

  and and_1 (R[0], A[0], B[0]);
  and and_2 (R[1], A[1], B[1]);
endmodule

module or2bit (
  input  [1:0] A,
  input  [1:0] B,
  output [1:0] R
);

  or or_1 (R[0], A[0], B[0]);
  or or_2 (R[1], A[1], B[1]);
endmodule

module xor2bit (
  input  [1:0] A,
  input  [1:0] B,
  output [1:0] R
);

  xor xor_1 (R[0], A[0], B[0]);
  xor xor_2 (R[1], A[1], B[1]);
endmodule

module leftshift2bit (
  input  [1:0] A,
  input  [1:0] B,
  output [1:0] R
);

  Multiplexer multiplexer_1 (.in0(A[1]), .in1(A[0]), .out(R[1]), .sel(B[0]));
  Multiplexer multiplexer_2 (.in0(A[0]), .in1(1'b0), .out(R[0]), .sel(B[0]));

  // Other names for the same wires on the sheet: Shift = B[0]
endmodule

module rightshift2bit (
  input  [1:0] A,
  input  [1:0] B,
  output [1:0] R
);

  Multiplexer multiplexer_1 (.in0(A[1]), .in1(1'b0), .out(R[1]), .sel(B[0]));
  Multiplexer multiplexer_2 (.in0(A[0]), .in1(A[1]), .out(R[0]), .sel(B[0]));

  // Other names for the same wires on the sheet: Sel = B[0]
endmodule

module fulladder1bit (
  input  A,
  input  B,
  input  Ci,
  output S,
  output Co
);

  wire and_1_out, and_2_out, xor_1_out;

  and and_1 (and_1_out, A, B);
  xor xor_1 (xor_1_out, A, B);
  and and_2 (and_2_out, xor_1_out, Ci);
  xor xor_2 (S, xor_1_out, Ci);
  or or_1 (Co, and_2_out, and_1_out);
endmodule

module addsub2bit (
  input  [1:0] A,
  input  [1:0] B,
  input  Add_sub_sel,
  output [1:0] R,
  output Co
);

  wire fulladder1bit_2_co, xor_1_out, xor_2_out;

  fulladder1bit fulladder1bit_1 (.A(A[1]), .B(xor_1_out), .Ci(fulladder1bit_2_co), .S(R[1]), .Co(Co));
  xor xor_1 (xor_1_out, Add_sub_sel, B[1]);
  xor xor_2 (xor_2_out, Add_sub_sel, B[0]);
  fulladder1bit fulladder1bit_2 (.A(A[0]), .B(xor_2_out), .Ci(Add_sub_sel), .S(R[0]), .Co(fulladder1bit_2_co));
endmodule

module leftrotate2bit (
  input  [1:0] A,
  input  [1:0] B,
  output [1:0] R
);

  Multiplexer multiplexer_1 (.in0(A[1]), .in1(A[0]), .out(R[1]), .sel(B[0]));
  Multiplexer multiplexer_2 (.in0(A[0]), .in1(A[1]), .out(R[0]), .sel(B[0]));

  // Other names for the same wires on the sheet: L_rotate = B[0]
endmodule

module rightrotate2bit (
  input  [1:0] A,
  input  [1:0] B,
  output [1:0] R
);

  Multiplexer multiplexer_1 (.in0(A[1]), .in1(A[0]), .out(R[1]), .sel(B[0]));
  Multiplexer multiplexer_2 (.in0(A[0]), .in1(A[1]), .out(R[0]), .sel(B[0]));

  // Other names for the same wires on the sheet: R_rotate = B[0]
endmodule

module not2bit (
  input  [1:0] A,
  output [1:0] R
);

  not not_1 (R[0], A[0]);
  not not_2 (R[1], A[1]);
endmodule

module alu2bit (
  input  [1:0] A,
  input  [1:0] B,
  input  [3:0] Sel,
  output [1:0] R,
  output Sign_flag,
  output Zero_flag,
  output Carry_flag
);

  wire or_1_out;
  wire [1:0] ANDr, Left_rotate, Left_shift, NOTr, Orr, Right_rotate, Right_shift, Sum_Sub, undriven, Xorr;

  and2bit and2bit_1 (.A(A), .B(B), .R(ANDr));
  or2bit or2bit_1 (.A(A), .B(B), .R(Orr));
  xor2bit xor2bit_1 (.A(A), .B(B), .R(Xorr));
  leftshift2bit leftshift2bit_1 (.B(B), .A(A), .R(Left_shift));
  rightshift2bit rightshift2bit_1 (.B(B), .A(A), .R(Right_shift));
  addsub2bit addsub2bit_1 (.B(B), .A(A), .Add_sub_sel(Sel[1]), .Co(Carry_flag), .R(Sum_Sub));
  leftrotate2bit leftrotate2bit_1 (.B(B), .A(A), .R(Left_rotate));
  rightrotate2bit rightrotate2bit_1 (.B(B), .A(A), .R(Right_rotate));
  not2bit not2bit_1 (.A(A), .R(NOTr));
  Multiplexer #(.select(4), .width(2)) multiplexer_1 (
    .in0(ANDr), .in1(Orr), .in2(Xorr), .in3(Left_shift), .in4(Right_shift), .in5(Sum_Sub), .in6(Sum_Sub),
    .in7(undriven), .in8(Left_rotate), .in9(Right_rotate), .in10(NOTr), .out(R), .sel(Sel));  // open: in11, in12, in13, in14, in15
  or or_1 (or_1_out, R[0], R[1]);
  not not_1 (Zero_flag, or_1_out);

  assign Sign_flag = R[1];

  // Other names for the same wires on the sheet: Add_Sub_sel = Sel[1]
endmodule
