// Logisim project alu3bit.circ as structural Verilog: 11 circuits, main circuit and3bit
module and3bit (
  input  [2:0] A,
  input  [2:0] B,
  output [2:0] R
);

  and and_1 (R[0], A[0], B[0]);
  and and_2 (R[1], A[1], B[1]);
  and and_3 (R[2], A[2], B[2]);
endmodule

module or3bit (
  input  [2:0] A,
  input  [2:0] B,
  output [2:0] R
);

  or or_1 (R[0], A[0], B[0]);
  or or_2 (R[1], A[1], B[1]);
  or or_3 (R[2], A[2], B[2]);
endmodule

module xor3bit (
  input  [2:0] A,
  input  [2:0] B,
  output [2:0] R
);

  xor xor_1 (R[0], A[0], B[0]);
  xor xor_2 (R[1], A[1], B[1]);
  xor xor_3 (R[2], A[2], B[2]);
endmodule

module leftshift3bit (
  input  [2:0] A,
  input  [2:0] B,
  output [2:0] R
);

  Multiplexer #(.select(2)) multiplexer_1 (.in0(A[2]), .in1(A[1]), .in2(A[0]), .out(R[2]), .sel(B[1:0]));  // open: in3
  Multiplexer #(.select(2)) multiplexer_2 (.in0(A[1]), .in1(A[0]), .in2(1'b0), .out(R[1]), .sel(B[1:0]));  // open: in3
  Multiplexer #(.select(2)) multiplexer_3 (.in0(A[0]), .in1(1'b0), .in2(1'b0), .out(R[0]), .sel(B[1:0]));  // open: in3

  // Other names for the same wires on the sheet: Sel[1:0] = B[1:0]
endmodule

module rightshift3bit (
  input  [2:0] A,
  input  [2:0] B,
  output [2:0] R
);

  Multiplexer #(.select(2)) multiplexer_1 (.in0(A[2]), .in1(1'b0), .in2(1'b0), .out(R[2]), .sel(B[1:0]));  // open: in3
  Multiplexer #(.select(2)) multiplexer_2 (.in0(A[1]), .in1(A[2]), .in2(1'b0), .out(R[1]), .sel(B[1:0]));  // open: in3
  Multiplexer #(.select(2)) multiplexer_3 (.in0(A[0]), .in1(A[1]), .in2(A[2]), .out(R[0]), .sel(B[1:0]));  // open: in3

  // Other names for the same wires on the sheet: Sel[1:0] = B[1:0]
endmodule

module fulladder1bit (
  input  A,
  input  B,
  input  Ci,
  output S,
  output Co
);

  wire and_1_out, and_2_out, xor_1_out;

  and and_1 (and_1_out, A, B);
  xor xor_1 (xor_1_out, A, B);
  and and_2 (and_2_out, xor_1_out, Ci);
  xor xor_2 (S, xor_1_out, Ci);
  or or_1 (Co, and_2_out, and_1_out);
endmodule

module addsub3bit (
  input  [2:0] A,
  input  [2:0] B,
  input  Add_Sub_sel,
  output [2:0] S,
  output Co
);

  wire fulladder1bit_2_co, fulladder1bit_3_co;

  fulladder1bit fulladder1bit_1 (.A(A[2]), .Ci(fulladder1bit_2_co), .S(S[2]), .Co(Co));  // open: B
  // XOR_Gate xor_1 has open pins: in0=Add_Sub_sel, in1=B[2], out=open
  fulladder1bit fulladder1bit_2 (.A(A[1]), .Ci(fulladder1bit_3_co), .S(S[1]), .Co(fulladder1bit_2_co));  // open: B
  // XOR_Gate xor_2 has open pins: in0=Add_Sub_sel, in1=B[1], out=open
  fulladder1bit fulladder1bit_3 (.A(A[0]), .Ci(Add_Sub_sel), .S(S[0]), .Co(fulladder1bit_3_co));  // open: B
  // XOR_Gate xor_3 has open pins: in0=Add_Sub_sel, in1=B[0], out=open
endmodule

module leftrotate3bit (
  input  [2:0] A,
  input  [2:0] B,
  output [2:0] R
);

  Multiplexer #(.select(2)) multiplexer_1 (.in0(A[2]), .in1(A[1]), .in2(A[0]), .out(R[2]), .sel(B[1:0]));  // open: in3
  Multiplexer #(.select(2)) multiplexer_2 (.in0(A[1]), .in1(A[0]), .in2(A[2]), .out(R[1]), .sel(B[1:0]));  // open: in3
  Multiplexer #(.select(2)) multiplexer_3 (.in0(A[0]), .in1(A[2]), .in2(A[1]), .out(R[0]), .sel(B[1:0]));  // open: in3

  // Other names for the same wires on the sheet: Sel[1:0] = B[1:0]
endmodule

module rightrotate3bit (
  input  [2:0] A,
  input  [2:0] B,
  output [2:0] R
);

  Multiplexer #(.select(2)) multiplexer_1 (.in0(A[2]), .in1(A[0]), .in2(A[1]), .out(R[2]), .sel(B[1:0]));  // open: in3
  Multiplexer #(.select(2)) multiplexer_2 (.in0(A[1]), .in1(A[2]), .in2(A[0]), .out(R[1]), .sel(B[1:0]));  // open: in3
  Multiplexer #(.select(2)) multiplexer_3 (.in0(A[0]), .in1(A[1]), .in2(A[2]), .out(R[0]), .sel(B[1:0]));  // open: in3

  // Other names for the same wires on the sheet: Sel[1:0] = B[1:0]
endmodule

module not3bit (
  input  [2:0] A,
  output [2:0] R
);

  not not_1 (R[0], A[0]);
  not not_2 (R[1], A[1]);
  not not_3 (R[2], A[2]);
endmodule

module alu3bit (
  input  [2:0] A,
  input  [2:0] B,
  input  [3:0] Sel,
  output [2:0] R,
  output Sign_flag,
  output Zero_flag,
  output Carry_flag
);

  wire or_1_out;
  wire [2:0] ANDr, Left_rotate, Left_shift, NOTr, Orr, Right_rotate, Right_shift, Sum_Sub, undriven, Xorr;

  and3bit and3bit_1 (.B(B), .A(A), .R(ANDr));
  or3bit or3bit_1 (.B(B), .A(A), .R(Orr));
  xor3bit xor3bit_1 (.B(B), .A(A), .R(Xorr));
  leftshift3bit leftshift3bit_1 (.A(A), .B(B), .R(Left_shift));
  rightshift3bit rightshift3bit_1 (.A(A), .B(B), .R(Right_shift));
  addsub3bit addsub3bit_1 (.B(B), .A(A), .Add_Sub_sel(Sel[1]), .Co(Carry_flag), .S(Sum_Sub));
  leftrotate3bit leftrotate3bit_1 (.A(A), .B(B), .R(Left_rotate));
  rightrotate3bit rightrotate3bit_1 (.A(A), .B(B), .R(Right_rotate));
  not3bit not3bit_1 (.A(A), .R(NOTr));
  Multiplexer #(.select(4), .width(3)) multiplexer_1 (
    .in0(ANDr), .in1(Orr), .in2(Xorr), .in3(Left_shift), .in4(Right_shift), .in5(Sum_Sub), .in6(Sum_Sub),
    .in7(undriven), .in8(Left_rotate), .in9(Right_rotate), .in10(NOTr), .out(R), .sel(Sel));  // open: in11, in12, in13, in14, in15
  or or_1 (or_1_out, R[0], R[1], R[2]);
  not not_1 (Zero_flag, or_1_out);

  assign Sign_flag = R[2];

  // Other names for the same wires on the sheet: Add_Sub_sel = Sel[1]
endmodule
