// Logisim project registerMasum.circ as structural Verilog: 24 circuits, main circuit register1bit
module register1bit (
  input  Din,
  input  Sel,
  input  CLK,
  output Dout
);

  wire multiplexer_1_out;

  Multiplexer multiplexer_1 (.in0(Dout), .in1(Din), .out(multiplexer_1_out), .sel(Sel));
  D_Flip_Flop d_ff_1 (.D(multiplexer_1_out), .clk(CLK), .Q(Dout));  // open: Qn, preset, reset
endmodule

module register2bit (
  input  [1:0] Din,
  input  Sel,
  input  CLK,
  output [1:0] R
);

  register1bit register1bit_1 (.Din(Din[0]), .Sel(Sel), .CLK(CLK), .Dout(R[0]));
  register1bit register1bit_2 (.Din(Din[1]), .Sel(Sel), .CLK(CLK), .Dout(R[1]));
endmodule

module register3bit (
  input  [2:0] A,
  input  Sel,
  input  CLK,
  output [2:0] R
);

  register1bit register1bit_1 (.Din(A[0]), .Sel(Sel), .CLK(CLK), .Dout(R[0]));
  register1bit register1bit_2 (.Din(A[1]), .Sel(Sel), .CLK(CLK), .Dout(R[1]));
  register1bit register1bit_3 (.Din(A[2]), .Sel(Sel), .CLK(CLK), .Dout(R[2]));
endmodule

module register4bit (
  input  [3:0] A,
  input  Sel,
  input  CLK,
  output [3:0] R
);

  register1bit register1bit_1 (.Din(A[0]), .Sel(Sel), .CLK(CLK), .Dout(R[0]));
  register1bit register1bit_2 (.Din(A[1]), .Sel(Sel), .CLK(CLK), .Dout(R[1]));
  register1bit register1bit_3 (.Din(A[2]), .Sel(Sel), .CLK(CLK), .Dout(R[2]));
  register1bit register1bit_4 (.Din(A[3]), .Sel(Sel), .CLK(CLK), .Dout(R[3]));
endmodule

module register5bit (
  input  [4:0] A,
  input  Sel,
  input  CLK,
  output [4:0] R
);

  register1bit register1bit_1 (.Din(A[0]), .Sel(Sel), .CLK(CLK), .Dout(R[0]));
  register1bit register1bit_2 (.Din(A[1]), .Sel(Sel), .CLK(CLK), .Dout(R[1]));
  register1bit register1bit_3 (.Din(A[2]), .Sel(Sel), .CLK(CLK), .Dout(R[2]));
  register1bit register1bit_4 (.Din(A[3]), .Sel(Sel), .CLK(CLK), .Dout(R[3]));
  register1bit register1bit_5 (.Din(A[4]), .Sel(Sel), .CLK(CLK), .Dout(R[4]));
endmodule

module register6bit (
  input  [5:0] A,
  input  Sel,
  input  CLK,
  output [5:0] R
);

  register1bit register1bit_1 (.Din(A[0]), .Sel(Sel), .CLK(CLK), .Dout(R[0]));
  register1bit register1bit_2 (.Din(A[1]), .Sel(Sel), .CLK(CLK), .Dout(R[1]));
  register1bit register1bit_3 (.Din(A[2]), .Sel(Sel), .CLK(CLK), .Dout(R[2]));
  register1bit register1bit_4 (.Din(A[3]), .Sel(Sel), .CLK(CLK), .Dout(R[3]));
  register1bit register1bit_5 (.Din(A[4]), .Sel(Sel), .CLK(CLK), .Dout(R[4]));
  register1bit register1bit_6 (.Din(A[5]), .Sel(Sel), .CLK(CLK), .Dout(R[5]));
endmodule

module register7bit (
  input  [6:0] A,
  input  Sel,
  input  CLK,
  output [6:0] R
);

  register1bit register1bit_1 (.Din(A[0]), .Sel(Sel), .CLK(CLK), .Dout(R[0]));
  register1bit register1bit_2 (.Din(A[1]), .Sel(Sel), .CLK(CLK), .Dout(R[1]));
  register1bit register1bit_3 (.Din(A[2]), .Sel(Sel), .CLK(CLK), .Dout(R[2]));
  register1bit register1bit_4 (.Din(A[3]), .Sel(Sel), .CLK(CLK), .Dout(R[3]));
  register1bit register1bit_5 (.Din(A[4]), .Sel(Sel), .CLK(CLK), .Dout(R[4]));
  register1bit register1bit_6 (.Din(A[5]), .Sel(Sel), .CLK(CLK), .Dout(R[5]));
  register1bit register1bit_7 (.Din(A[6]), .Sel(Sel), .CLK(CLK), .Dout(R[6]));
endmodule

module register8bit (
  input  [7:0] A,
  input  Sel,
  input  CLK,
  output [7:0] R
);

  register1bit register1bit_1 (.Din(A[0]), .Sel(Sel), .CLK(CLK), .Dout(R[0]));
  register1bit register1bit_2 (.Din(A[1]), .Sel(Sel), .CLK(CLK), .Dout(R[1]));
  register1bit register1bit_3 (.Din(A[2]), .Sel(Sel), .CLK(CLK), .Dout(R[2]));
  register1bit register1bit_4 (.Din(A[3]), .Sel(Sel), .CLK(CLK), .Dout(R[3]));
  register1bit register1bit_5 (.Din(A[4]), .Sel(Sel), .CLK(CLK), .Dout(R[4]));
  register1bit register1bit_6 (.Din(A[5]), .Sel(Sel), .CLK(CLK), .Dout(R[5]));
  register1bit register1bit_7 (.Din(A[6]), .Sel(Sel), .CLK(CLK), .Dout(R[6]));
  register1bit register1bit_8 (.Din(A[7]), .Sel(Sel), .CLK(CLK), .Dout(R[7]));
endmodule

module register9bit (
  input  [8:0] in_1,
  input  Sel,
  input  CLK,
  output [8:0] R
);

  register1bit register1bit_1 (.Din(in_1[0]), .Sel(Sel), .CLK(CLK), .Dout(R[0]));
  register1bit register1bit_2 (.Din(in_1[1]), .Sel(Sel), .CLK(CLK), .Dout(R[1]));
  register1bit register1bit_3 (.Din(in_1[2]), .Sel(Sel), .CLK(CLK), .Dout(R[2]));
  register1bit register1bit_4 (.Din(in_1[3]), .Sel(Sel), .CLK(CLK), .Dout(R[3]));
  register1bit register1bit_5 (.Din(in_1[4]), .Sel(Sel), .CLK(CLK), .Dout(R[4]));
  register1bit register1bit_6 (.Din(in_1[5]), .Sel(Sel), .CLK(CLK), .Dout(R[5]));
  register1bit register1bit_7 (.Din(in_1[6]), .Sel(Sel), .CLK(CLK), .Dout(R[6]));
  register1bit register1bit_8 (.Din(in_1[7]), .Sel(Sel), .CLK(CLK), .Dout(R[7]));
  register1bit register1bit_9 (.Din(in_1[8]), .Sel(Sel), .CLK(CLK), .Dout(R[8]));
endmodule

module register10bit (
  input  [9:0] in_1,
  input  Sel,
  input  CLK,
  output [9:0] R
);

  register1bit register1bit_1 (.Din(in_1[0]), .Sel(Sel), .CLK(CLK), .Dout(R[0]));
  register1bit register1bit_2 (.Din(in_1[1]), .Sel(Sel), .CLK(CLK), .Dout(R[1]));
  register1bit register1bit_3 (.Din(in_1[2]), .Sel(Sel), .CLK(CLK), .Dout(R[2]));
  register1bit register1bit_4 (.Din(in_1[3]), .Sel(Sel), .CLK(CLK), .Dout(R[3]));
  register1bit register1bit_5 (.Din(in_1[4]), .Sel(Sel), .CLK(CLK), .Dout(R[4]));
  register1bit register1bit_6 (.Din(in_1[5]), .Sel(Sel), .CLK(CLK), .Dout(R[5]));
  register1bit register1bit_7 (.Din(in_1[6]), .Sel(Sel), .CLK(CLK), .Dout(R[6]));
  register1bit register1bit_8 (.Din(in_1[7]), .Sel(Sel), .CLK(CLK), .Dout(R[7]));
  register1bit register1bit_9 (.Din(in_1[8]), .Sel(Sel), .CLK(CLK), .Dout(R[8]));
  register1bit register1bit_10 (.Din(in_1[9]), .Sel(Sel), .CLK(CLK), .Dout(R[9]));
endmodule

module register2bit1 (
  input  Ra,
  input  Reg_en,
  input  Wr,
  input  [1:0] Wrd,
  input  CLK,
  input  Rb,
  output [1:0] A,
  output [1:0] B
);

  wire decoder_1_out0;
  wire [1:0] register2bit_1_r;

  Decoder decoder_1 (.out0(decoder_1_out0), .sel(Wr), .en(Reg_en));  // open: out1
  register2bit register2bit_1 (.Din(Wrd), .Sel(decoder_1_out0), .CLK(CLK), .R(register2bit_1_r));
  Multiplexer #(.width(2)) multiplexer_1 (.in0(register2bit_1_r), .out(A), .sel(Ra));  // open: in1
  Multiplexer #(.width(2)) multiplexer_2 (.in0(register2bit_1_r), .out(B), .sel(Rb));  // open: in1
endmodule

module register2bit2 (
  input  Ra,
  input  Reg_en,
  input  Wr,
  input  [1:0] Wrd,
  input  CLK,
  input  Rb,
  output [1:0] A,
  output [1:0] B
);

  wire decoder_1_out0, decoder_1_out1;
  wire [1:0] register2bit_1_r, register2bit_2_r;

  Decoder decoder_1 (.out0(decoder_1_out0), .out1(decoder_1_out1), .sel(Wr), .en(Reg_en));
  register2bit register2bit_1 (.Din(Wrd), .Sel(decoder_1_out0), .CLK(CLK), .R(register2bit_1_r));
  register2bit register2bit_2 (.Din(Wrd), .Sel(decoder_1_out1), .CLK(CLK), .R(register2bit_2_r));
  Multiplexer #(.width(2)) multiplexer_1 (.in0(register2bit_1_r), .in1(register2bit_2_r), .out(A), .sel(Ra));
  Multiplexer #(.width(2)) multiplexer_2 (.in0(register2bit_1_r), .in1(register2bit_2_r), .out(B), .sel(Rb));
endmodule

module register2bit3 (
  input  [1:0] Ra,
  input  Reg_en,
  input  [1:0] Wr,
  input  [1:0] Wrd,
  input  [1:0] Rb,
  input  CLK,
  output [1:0] A,
  output [1:0] B
);

  wire decoder_1_out0, decoder_1_out1, decoder_1_out2;
  wire [1:0] register2bit_1_r, register2bit_2_r, register2bit_3_r;

  Decoder #(.select(2)) decoder_1 (
    .out0(decoder_1_out0), .out1(decoder_1_out1), .out2(decoder_1_out2), .sel(Wr), .en(Reg_en));  // open: out3
  register2bit register2bit_1 (.Din(Wrd), .Sel(decoder_1_out0), .CLK(CLK), .R(register2bit_1_r));
  register2bit register2bit_2 (.Din(Wrd), .Sel(decoder_1_out1), .CLK(CLK), .R(register2bit_2_r));
  register2bit register2bit_3 (.Din(Wrd), .Sel(decoder_1_out2), .CLK(CLK), .R(register2bit_3_r));
  Multiplexer #(.select(2), .width(2)) multiplexer_1 (
    .in0(register2bit_1_r), .in1(register2bit_2_r), .in2(register2bit_3_r), .out(A), .sel(Ra));  // open: in3
  Multiplexer #(.select(2), .width(2)) multiplexer_2 (
    .in0(register2bit_1_r), .in1(register2bit_2_r), .in2(register2bit_3_r), .out(B), .sel(Rb));  // open: in3
endmodule

module register2bit4 (
  input  [1:0] Ra,
  input  Reg_en,
  input  [1:0] Wr,
  input  [1:0] Rb,
  input  [1:0] Wrd,
  input  CLK,
  output [1:0] A,
  output [1:0] B
);

  wire decoder_1_out0, decoder_1_out1, decoder_1_out2, decoder_1_out3;
  wire [1:0] register2bit_1_r, register2bit_2_r, register2bit_3_r, register2bit_4_r;

  Decoder #(.select(2)) decoder_1 (
    .out0(decoder_1_out0), .out1(decoder_1_out1), .out2(decoder_1_out2), .out3(decoder_1_out3), .sel(Wr),
    .en(Reg_en));
  register2bit register2bit_1 (.Din(Wrd), .Sel(decoder_1_out0), .CLK(CLK), .R(register2bit_1_r));
  register2bit register2bit_2 (.Din(Wrd), .Sel(decoder_1_out1), .CLK(CLK), .R(register2bit_2_r));
  register2bit register2bit_3 (.Din(Wrd), .Sel(decoder_1_out2), .CLK(CLK), .R(register2bit_3_r));
  register2bit register2bit_4 (.Din(Wrd), .Sel(decoder_1_out3), .CLK(CLK), .R(register2bit_4_r));
  Multiplexer #(.select(2), .width(2)) multiplexer_1 (
    .in0(register2bit_1_r), .in1(register2bit_2_r), .in2(register2bit_3_r), .in3(register2bit_4_r), .out(A),
    .sel(Ra));
  Multiplexer #(.select(2), .width(2)) multiplexer_2 (
    .in0(register2bit_1_r), .in1(register2bit_2_r), .in2(register2bit_3_r), .in3(register2bit_4_r), .out(B),
    .sel(Rb));
endmodule

module register2bit5 (
  input  [2:0] Ra,
  input  Reg_en,
  input  [2:0] Wr,
  input  [2:0] Rb,
  input  [1:0] Wrd,
  input  CLK,
  output [1:0] A,
  output [1:0] B
);

  wire decoder_1_out0, decoder_1_out1, decoder_1_out2, decoder_1_out3, decoder_1_out4;
  wire [1:0] register2bit_1_r, register2bit_2_r, register2bit_3_r, register2bit_4_r, register2bit_5_r;

  Decoder #(.select(3)) decoder_1 (
    .out0(decoder_1_out0), .out1(decoder_1_out1), .out2(decoder_1_out2), .out3(decoder_1_out3),
    .out4(decoder_1_out4), .sel(Wr), .en(Reg_en));  // open: out5, out6, out7
  register2bit register2bit_1 (.Din(Wrd), .Sel(decoder_1_out0), .CLK(CLK), .R(register2bit_1_r));
  register2bit register2bit_2 (.Din(Wrd), .Sel(decoder_1_out1), .CLK(CLK), .R(register2bit_2_r));
  register2bit register2bit_3 (.Din(Wrd), .Sel(decoder_1_out2), .CLK(CLK), .R(register2bit_3_r));
  register2bit register2bit_4 (.Din(Wrd), .Sel(decoder_1_out3), .CLK(CLK), .R(register2bit_4_r));
  register2bit register2bit_5 (.Din(Wrd), .Sel(decoder_1_out4), .CLK(CLK), .R(register2bit_5_r));
  Multiplexer #(.select(3), .width(2)) multiplexer_1 (
    .in0(register2bit_1_r), .in1(register2bit_2_r), .in2(register2bit_3_r), .in3(register2bit_4_r),
    .in4(register2bit_5_r), .out(A), .sel(Ra));  // open: in5, in6, in7
  Multiplexer #(.select(3), .width(2)) multiplexer_2 (
    .in0(register2bit_1_r), .in1(register2bit_2_r), .in2(register2bit_3_r), .in3(register2bit_4_r),
    .in4(register2bit_5_r), .out(B), .sel(Rb));  // open: in5, in6, in7
endmodule

module register2bit6 (
  input  [2:0] Ra,
  input  Reg_en,
  input  [2:0] Wr,
  input  [2:0] Rb,
  input  [1:0] Wrd,
  input  CLK,
  output [1:0] A,
  output [1:0] B
);

  wire decoder_1_out0, decoder_1_out1, decoder_1_out2, decoder_1_out3, decoder_1_out4, decoder_1_out5;
  wire [1:0] register2bit_1_r, register2bit_2_r, register2bit_3_r, register2bit_4_r, register2bit_5_r,
       register2bit_6_r;

  Decoder #(.select(3)) decoder_1 (
    .out0(decoder_1_out0), .out1(decoder_1_out1), .out2(decoder_1_out2), .out3(decoder_1_out3),
    .out4(decoder_1_out4), .out5(decoder_1_out5), .sel(Wr), .en(Reg_en));  // open: out6, out7
  register2bit register2bit_1 (.Din(Wrd), .Sel(decoder_1_out0), .CLK(CLK), .R(register2bit_1_r));
  register2bit register2bit_2 (.Din(Wrd), .Sel(decoder_1_out1), .CLK(CLK), .R(register2bit_2_r));
  register2bit register2bit_3 (.Din(Wrd), .Sel(decoder_1_out2), .CLK(CLK), .R(register2bit_3_r));
  register2bit register2bit_4 (.Din(Wrd), .Sel(decoder_1_out3), .CLK(CLK), .R(register2bit_4_r));
  register2bit register2bit_5 (.Din(Wrd), .Sel(decoder_1_out4), .CLK(CLK), .R(register2bit_5_r));
  register2bit register2bit_6 (.Din(Wrd), .Sel(decoder_1_out5), .CLK(CLK), .R(register2bit_6_r));
  Multiplexer #(.select(3), .width(2)) multiplexer_1 (
    .in0(register2bit_1_r), .in1(register2bit_2_r), .in2(register2bit_3_r), .in3(register2bit_4_r),
    .in4(register2bit_5_r), .in5(register2bit_6_r), .out(A), .sel(Ra));  // open: in6, in7
  Multiplexer #(.select(3), .width(2)) multiplexer_2 (
    .in0(register2bit_1_r), .in1(register2bit_2_r), .in2(register2bit_3_r), .in3(register2bit_4_r),
    .in4(register2bit_5_r), .in5(register2bit_6_r), .out(B), .sel(Rb));  // open: in6, in7
endmodule

module register2bit7 (
  input  [2:0] Ra,
  input  Reg_en,
  input  [2:0] Wr,
  input  [2:0] Rb,
  input  [1:0] Wrd,
  input  CLK,
  output [1:0] A,
  output [1:0] B
);

  wire decoder_1_out0, decoder_1_out1, decoder_1_out2, decoder_1_out3, decoder_1_out4, decoder_1_out5,
       decoder_1_out6;
  wire [1:0] register2bit_1_r, register2bit_2_r, register2bit_3_r, register2bit_4_r, register2bit_5_r,
       register2bit_6_r, register2bit_7_r;

  Decoder #(.select(3)) decoder_1 (
    .out0(decoder_1_out0), .out1(decoder_1_out1), .out2(decoder_1_out2), .out3(decoder_1_out3),
    .out4(decoder_1_out4), .out5(decoder_1_out5), .out6(decoder_1_out6), .sel(Wr), .en(Reg_en));  // open: out7
  register2bit register2bit_1 (.Din(Wrd), .Sel(decoder_1_out0), .CLK(CLK), .R(register2bit_1_r));
  register2bit register2bit_2 (.Din(Wrd), .Sel(decoder_1_out1), .CLK(CLK), .R(register2bit_2_r));
  register2bit register2bit_3 (.Din(Wrd), .Sel(decoder_1_out2), .CLK(CLK), .R(register2bit_3_r));
  register2bit register2bit_4 (.Din(Wrd), .Sel(decoder_1_out3), .CLK(CLK), .R(register2bit_4_r));
  register2bit register2bit_5 (.Din(Wrd), .Sel(decoder_1_out4), .CLK(CLK), .R(register2bit_5_r));
  register2bit register2bit_6 (.Din(Wrd), .Sel(decoder_1_out5), .CLK(CLK), .R(register2bit_6_r));
  register2bit register2bit_7 (.Din(Wrd), .Sel(decoder_1_out6), .CLK(CLK), .R(register2bit_7_r));
  Multiplexer #(.select(3), .width(2)) multiplexer_1 (
    .in0(register2bit_1_r), .in1(register2bit_2_r), .in2(register2bit_3_r), .in3(register2bit_4_r),
    .in4(register2bit_5_r), .in5(register2bit_6_r), .in6(register2bit_7_r), .out(A), .sel(Ra));  // open: in7
  Multiplexer #(.select(3), .width(2)) multiplexer_2 (
    .in0(register2bit_1_r), .in1(register2bit_2_r), .in2(register2bit_3_r), .in3(register2bit_4_r),
    .in4(register2bit_5_r), .in5(register2bit_6_r), .in6(register2bit_7_r), .out(B), .sel(Rb));  // open: in7
endmodule

module register2bit8 (
  input  [2:0] Ra,
  input  Reg_en,
  input  [2:0] Wr,
  input  [2:0] Rb,
  input  [1:0] Wrd,
  input  CLK,
  output [1:0] A,
  output [1:0] B
);

  wire decoder_1_out0, decoder_1_out1, decoder_1_out2, decoder_1_out3, decoder_1_out4, decoder_1_out5,
       decoder_1_out6, decoder_1_out7;
  wire [1:0] register2bit_1_r, register2bit_2_r, register2bit_3_r, register2bit_4_r, register2bit_5_r,
       register2bit_6_r, register2bit_7_r, register2bit_8_r;

  Decoder #(.select(3)) decoder_1 (
    .out0(decoder_1_out0), .out1(decoder_1_out1), .out2(decoder_1_out2), .out3(decoder_1_out3),
    .out4(decoder_1_out4), .out5(decoder_1_out5), .out6(decoder_1_out6), .out7(decoder_1_out7), .sel(Wr),
    .en(Reg_en));
  register2bit register2bit_1 (.Din(Wrd), .Sel(decoder_1_out0), .CLK(CLK), .R(register2bit_1_r));
  register2bit register2bit_2 (.Din(Wrd), .Sel(decoder_1_out1), .CLK(CLK), .R(register2bit_2_r));
  register2bit register2bit_3 (.Din(Wrd), .Sel(decoder_1_out2), .CLK(CLK), .R(register2bit_3_r));
  register2bit register2bit_4 (.Din(Wrd), .Sel(decoder_1_out3), .CLK(CLK), .R(register2bit_4_r));
  register2bit register2bit_5 (.Din(Wrd), .Sel(decoder_1_out4), .CLK(CLK), .R(register2bit_5_r));
  register2bit register2bit_6 (.Din(Wrd), .Sel(decoder_1_out5), .CLK(CLK), .R(register2bit_6_r));
  register2bit register2bit_7 (.Din(Wrd), .Sel(decoder_1_out6), .CLK(CLK), .R(register2bit_7_r));
  register2bit register2bit_8 (.Din(Wrd), .Sel(decoder_1_out7), .CLK(CLK), .R(register2bit_8_r));
  Multiplexer #(.select(3), .width(2)) multiplexer_1 (
    .in0(register2bit_1_r), .in1(register2bit_2_r), .in2(register2bit_3_r), .in3(register2bit_4_r),
    .in4(register2bit_5_r), .in5(register2bit_6_r), .in6(register2bit_7_r), .in7(register2bit_8_r), .out(A),
    .sel(Ra));
  Multiplexer #(.select(3), .width(2)) multiplexer_2 (
    .in0(register2bit_1_r), .in1(register2bit_2_r), .in2(register2bit_3_r), .in3(register2bit_4_r),
    .in4(register2bit_5_r), .in5(register2bit_6_r), .in6(register2bit_7_r), .in7(register2bit_8_r), .out(B),
    .sel(Rb));
endmodule

module register3bit1 (
  input  Ra,
  input  Reg_en,
  input  Wr,
  input  [2:0] Wrd,
  input  CLK,
  input  Rb,
  output [2:0] A,
  output [2:0] B
);

  wire decoder_1_out0;
  wire [2:0] register3bit_1_r;

  Decoder decoder_1 (.out0(decoder_1_out0), .sel(Wr), .en(Reg_en));  // open: out1
  register3bit register3bit_1 (.Sel(decoder_1_out0), .CLK(CLK), .A(Wrd), .R(register3bit_1_r));
  Multiplexer #(.width(3)) multiplexer_1 (.in0(register3bit_1_r), .out(A), .sel(Ra));  // open: in1
  Multiplexer #(.width(3)) multiplexer_2 (.in0(register3bit_1_r), .out(B), .sel(Rb));  // open: in1
endmodule

module register3bit2 (
  input  Ra,
  input  Reg_en,
  input  Wr,
  input  [2:0] Wrd,
  input  CLK,
  input  Rb,
  output [2:0] A,
  output [2:0] B
);

  wire decoder_1_out0, decoder_1_out1;
  wire [2:0] register3bit_1_r, register3bit_2_r;

  Decoder decoder_1 (.out0(decoder_1_out0), .out1(decoder_1_out1), .sel(Wr), .en(Reg_en));
  register3bit register3bit_1 (.Sel(decoder_1_out0), .CLK(CLK), .A(Wrd), .R(register3bit_1_r));
  register3bit register3bit_2 (.Sel(decoder_1_out1), .CLK(CLK), .A(Wrd), .R(register3bit_2_r));
  Multiplexer #(.width(3)) multiplexer_1 (.in0(register3bit_1_r), .in1(register3bit_2_r), .out(A), .sel(Ra));
  Multiplexer #(.width(3)) multiplexer_2 (.in0(register3bit_1_r), .in1(register3bit_2_r), .out(B), .sel(Rb));
endmodule

module register3bit3 (
  input  [1:0] Ra,
  input  Reg_en,
  input  [1:0] Wr,
  input  [2:0] Wrd,
  input  [1:0] Rb,
  input  CLK,
  output [2:0] A,
  output [2:0] B
);

  wire decoder_1_out0, decoder_1_out1, decoder_1_out2;
  wire [2:0] register3bit_1_r, register3bit_2_r, register3bit_3_r;

  Decoder #(.select(2)) decoder_1 (
    .out0(decoder_1_out0), .out1(decoder_1_out1), .out2(decoder_1_out2), .sel(Wr), .en(Reg_en));  // open: out3
  register3bit register3bit_1 (.Sel(decoder_1_out0), .CLK(CLK), .A(Wrd), .R(register3bit_1_r));
  register3bit register3bit_2 (.Sel(decoder_1_out1), .CLK(CLK), .A(Wrd), .R(register3bit_2_r));
  register3bit register3bit_3 (.Sel(decoder_1_out2), .CLK(CLK), .A(Wrd), .R(register3bit_3_r));
  Multiplexer #(.select(2), .width(3)) multiplexer_1 (
    .in0(register3bit_1_r), .in1(register3bit_2_r), .in2(register3bit_3_r), .out(A), .sel(Ra));  // open: in3
  Multiplexer #(.select(2), .width(3)) multiplexer_2 (
    .in0(register3bit_1_r), .in1(register3bit_2_r), .in2(register3bit_3_r), .out(B), .sel(Rb));  // open: in3
endmodule

module SRAM1x1 (
  input  Read_sel1,
  input  Write_data,
  input  Write_Sel,
  input  CLK,
  input  Read_sel2,
  output Read_data1,
  output Read_data2
);

  wire d_ff_1_q, multiplexer_1_out;

  Multiplexer multiplexer_1 (.in0(d_ff_1_q), .in1(Write_data), .out(multiplexer_1_out), .sel(Write_Sel));
  D_Flip_Flop d_ff_1 (.D(multiplexer_1_out), .clk(CLK), .Q(d_ff_1_q));  // open: Qn, preset, reset
  and and_1 (Read_data1, Read_sel1, d_ff_1_q);
  and and_2 (Read_data2, d_ff_1_q, Read_sel2);
endmodule

module SRAM1x3 (
  input  [2:0] Wd,
  input  RS1,
  input  RS2,
  input  WS,
  input  CLK,
  output [2:0] RD1,
  output [2:0] RD2
);

  SRAM1x1 sram1x1_1 (
    .Write_data(Wd[0]), .Write_Sel(WS), .CLK(CLK), .Read_sel2(RS2), .Read_sel1(RS1), .Read_data1(RD1[0]),
    .Read_data2(RD2[0]));
  SRAM1x1 sram1x1_2 (
    .Write_data(Wd[1]), .Write_Sel(WS), .CLK(CLK), .Read_sel2(RS2), .Read_sel1(RS1), .Read_data1(RD1[1]),
    .Read_data2(RD2[1]));
  SRAM1x1 sram1x1_3 (
    .Write_data(Wd[2]), .Write_Sel(WS), .CLK(CLK), .Read_sel2(RS2), .Read_sel1(RS1), .Read_data1(RD1[2]),
    .Read_data2(RD2[2]));
endmodule

module SRAM4x3 (
  input  WE,
  input  [1:0] WA,
  input  [2:0] Wrd,
  input  [1:0] RA1,
  input  [1:0] RA2,
  input  CLK,
  output [2:0] RD1,
  output [2:0] RD2
);

  wire decoder_1_out0, decoder_1_out1, decoder_1_out2, decoder_1_out3, decoder_2_out0, decoder_2_out1,
       decoder_2_out2, decoder_2_out3, decoder_3_out0, decoder_3_out1, decoder_3_out2, decoder_3_out3;
  wire [2:0] sram1x3_1_rd1, sram1x3_1_rd2, sram1x3_2_rd1, sram1x3_2_rd2, sram1x3_3_rd1, sram1x3_3_rd2,
       sram1x3_4_rd1, sram1x3_4_rd2;

  Decoder #(.select(2)) decoder_1 (
    .out0(decoder_1_out0), .out1(decoder_1_out1), .out2(decoder_1_out2), .out3(decoder_1_out3), .sel(WA),
    .en(WE));
  Decoder #(.select(2)) decoder_2 (
    .out0(decoder_2_out0), .out1(decoder_2_out1), .out2(decoder_2_out2), .out3(decoder_2_out3), .sel(RA1));  // open: en
  Decoder #(.select(2)) decoder_3 (
    .out0(decoder_3_out0), .out1(decoder_3_out1), .out2(decoder_3_out2), .out3(decoder_3_out3), .sel(RA2));  // open: en
  SRAM1x3 sram1x3_1 (
    .Wd(Wrd), .RS1(decoder_2_out0), .RS2(decoder_3_out0), .WS(decoder_1_out0), .CLK(CLK),
    .RD1(sram1x3_1_rd1), .RD2(sram1x3_1_rd2));
  SRAM1x3 sram1x3_2 (
    .Wd(Wrd), .RS1(decoder_2_out1), .RS2(decoder_3_out1), .WS(decoder_1_out1), .CLK(CLK),
    .RD1(sram1x3_2_rd1), .RD2(sram1x3_2_rd2));
  SRAM1x3 sram1x3_3 (
    .Wd(Wrd), .RS1(decoder_2_out2), .RS2(decoder_3_out2), .WS(decoder_1_out2), .CLK(CLK),
    .RD1(sram1x3_3_rd1), .RD2(sram1x3_3_rd2));
  SRAM1x3 sram1x3_4 (
    .Wd(Wrd), .RS1(decoder_2_out3), .RS2(decoder_3_out3), .WS(decoder_1_out3), .CLK(CLK),
    .RD1(sram1x3_4_rd1), .RD2(sram1x3_4_rd2));
  assign RD1 = sram1x3_1_rd1 | sram1x3_2_rd1 | sram1x3_3_rd1 | sram1x3_4_rd1;  // OR_Gate or_1, 3 bits wide
  assign RD2 = sram1x3_1_rd2 | sram1x3_2_rd2 | sram1x3_3_rd2 | sram1x3_4_rd2;  // OR_Gate or_2, 3 bits wide
endmodule
