// Logisim project NMOS AND CMOS TECH.circ as structural Verilog: 4 circuits, main circuit NMOS
module NMOS (
  input  in_1,
  input  X,
  input  Y,
  input  in_4,
  input  in_5,
  input  A,
  input  in_7,
  input  in_8,
  input  in_9,
  input  in_10,
  input  in_11,
  input  in_12,
  input  in_13,
  input  in_14,
  input  C,
  input  in_16,
  input  in_17,
  output out_18,
  output out_19,
  output W,
  output Z,
  output out_22,
  output out_23,
  output out_24,
  output out_25,
  output out_26,
  output out_27
);

  wire pull_resistor_4_node, pull_resistor_7_node, pull_resistor_9_node, pull_resistor_10_node,
       pull_resistor_11_node, pull_resistor_12_node, pull_resistor_13_node, transistor_7_out,
       transistor_10_out, transistor_15_out, transistor_18_out, transistor_20_out, transistor_22_out,
       transistor_26_out, transistor_27_out;

  Pull_Resistor #(.pull(1)) pull_resistor_1 (.node(Z));
  Transistor #(.\type ("n")) transistor_1 (.in(1'b0), .out(Z), .gate(A));
  Pull_Resistor #(.pull(1)) pull_resistor_2 (.node(out_23));
  Transistor #(.\type ("n")) transistor_2 (.in(1'b0), .out(out_23), .gate(C));
  Transistor #(.\type ("n")) transistor_3 (.in(1'b0), .out(W), .gate(X));
  Pull_Resistor #(.pull(1)) pull_resistor_3 (.node(W));
  Transistor #(.\type ("n")) transistor_4 (.in(1'b0), .out(W), .gate(Y));
  Pull_Resistor #(.pull(1)) pull_resistor_4 (.node(pull_resistor_4_node));
  Transistor transistor_5 (.in(pull_resistor_4_node), .out(out_25), .gate(in_12));
  Transistor #(.\type ("n")) transistor_6 (.in(1'b0), .out(out_25), .gate(in_12));
  Transistor #(.\type ("n")) transistor_7 (.in(1'b0), .out(transistor_7_out), .gate(in_4));
  Pull_Resistor #(.pull(1)) pull_resistor_5 (.node(transistor_7_out));
  Transistor #(.\type ("n")) transistor_8 (.in(1'b0), .out(transistor_7_out), .gate(in_7));
  Pull_Resistor #(.pull(1)) pull_resistor_6 (.node(out_19));
  Transistor #(.\type ("n")) transistor_9 (.in(1'b0), .out(out_19), .gate(transistor_7_out));
  Pull_Resistor #(.pull(1)) pull_resistor_7 (.node(pull_resistor_7_node));
  Transistor transistor_10 (.in(pull_resistor_7_node), .out(transistor_10_out), .gate(in_8));
  Transistor transistor_11 (.in(transistor_10_out), .out(out_22), .gate(in_16));
  Transistor #(.\type ("n")) transistor_12 (.in(1'b0), .out(out_22), .gate(in_8));
  Transistor #(.\type ("n")) transistor_13 (.in(1'b0), .out(out_22), .gate(in_16));
  Pull_Resistor #(.pull(1)) pull_resistor_8 (.node(out_18));
  Transistor #(.\type ("n")) transistor_14 (.in(transistor_15_out), .out(out_18), .gate(in_1));
  Transistor #(.\type ("n")) transistor_15 (.in(1'b0), .out(transistor_15_out), .gate(in_5));
  Transistor transistor_16 (.in(pull_resistor_9_node), .out(out_27), .gate(in_10));
  Pull_Resistor #(.pull(1)) pull_resistor_9 (.node(pull_resistor_9_node));
  Transistor #(.\type ("n")) transistor_17 (.in(transistor_18_out), .out(out_27), .gate(in_10));
  Transistor #(.\type ("n")) transistor_18 (.in(1'b0), .out(transistor_18_out), .gate(in_13));
  Transistor transistor_19 (.in(pull_resistor_9_node), .out(out_27), .gate(in_13));
  Transistor transistor_20 (.in(pull_resistor_10_node), .out(transistor_20_out), .gate(in_11));
  Pull_Resistor #(.pull(1)) pull_resistor_10 (.node(pull_resistor_10_node));
  Transistor #(.\type ("n")) transistor_21 (.in(transistor_22_out), .out(transistor_20_out), .gate(in_11));
  Transistor #(.\type ("n")) transistor_22 (.in(1'b0), .out(transistor_22_out), .gate(in_14));
  Transistor transistor_23 (.in(pull_resistor_10_node), .out(transistor_20_out), .gate(in_14));
  Pull_Resistor #(.pull(1)) pull_resistor_11 (.node(pull_resistor_11_node));
  Transistor transistor_24 (.in(pull_resistor_11_node), .out(out_26), .gate(transistor_20_out));
  Transistor #(.\type ("n")) transistor_25 (.in(1'b0), .out(out_26), .gate(transistor_20_out));
  Transistor #(.\type ("n")) transistor_26 (.in(1'b0), .out(transistor_26_out), .gate(in_9));
  Pull_Resistor #(.pull(1)) pull_resistor_12 (.node(pull_resistor_12_node));
  Transistor transistor_27 (.in(pull_resistor_12_node), .out(transistor_27_out), .gate(in_9));
  Transistor transistor_28 (.in(transistor_27_out), .out(transistor_26_out), .gate(in_17));
  Transistor #(.\type ("n")) transistor_29 (.in(1'b0), .out(transistor_26_out), .gate(in_17));
  Pull_Resistor #(.pull(1)) pull_resistor_13 (.node(pull_resistor_13_node));
  Transistor transistor_30 (.in(pull_resistor_13_node), .out(out_24), .gate(transistor_26_out));
  Transistor #(.\type ("n")) transistor_31 (.in(1'b0), .out(out_24), .gate(transistor_26_out));

  // Notes on the sheet:
  //   NMOS
  //   Inverter
  //   NOR GATE
  //   Inverter
  //   OR GATE
  //   NOR
  //   NAND
  //   NAND
  //   AND
  //   OR
endmodule

module Adder_1_bit (
  input  A,
  input  B,
  input  Cin,
  output S,
  output Co
);

  wire and_1_out, and_2_out, xor_1_out;

  xor xor_1 (xor_1_out, A, B);
  xor xor_2 (S, xor_1_out, Cin);
  and and_1 (and_1_out, xor_1_out, Cin);
  and and_2 (and_2_out, A, B);
  or or_1 (Co, and_1_out, and_2_out);

  // Notes on the sheet:
  //   1-Bit Full Adder
endmodule

module ADDER_4_bit (
  input  [3:0] B,
  input  [3:0] A,
  input  in_3,
  output Co,
  output [3:0] S
);

  wire FA1_co, FA2_co, FA3_co;

  Adder_1_bit FA4 (.A(A[3]), .B(B[3]), .Cin(FA3_co), .S(S[3]), .Co(Co));
  Adder_1_bit FA3 (.A(A[2]), .B(B[2]), .Cin(FA2_co), .S(S[2]), .Co(FA3_co));
  Adder_1_bit FA2 (.A(A[1]), .B(B[1]), .Cin(FA1_co), .S(S[1]), .Co(FA2_co));
  Adder_1_bit FA1 (.A(A[0]), .B(B[0]), .Cin(in_3), .S(S[0]), .Co(FA1_co));

  // Notes on the sheet:
  //   4-Bit Full Adder Using 1-Bit Full Adder
endmodule

module Adder_8_bit (
  input  [3:0] B1,
  input  [3:0] B2,
  input  [3:0] A1,
  input  [3:0] A2,
  input  in_5,
  output Co,
  output [3:0] Z1,
  output [3:0] Z2
);

  wire adder_4_bit_2_co;

  ADDER_4_bit adder_4_bit_1 (.A(A2), .B(B2), .in_3(adder_4_bit_2_co), .Co(Co), .S(Z1));
  ADDER_4_bit adder_4_bit_2 (.A(A1), .B(B1), .in_3(in_5), .Co(adder_4_bit_2_co), .S(Z2));

  // Notes on the sheet:
  //   8-Bit Full Adder Using 4-Bit Full Adder
endmodule
