// Logisim project ALU_4bit.circ as structural Verilog: 14 circuits, main circuit NMOS
module NMOS (
  input  in_1,
  input  X,
  input  Y,
  input  in_4,
  input  in_5,
  input  A,
  input  in_7,
  input  in_8,
  input  in_9,
  input  in_10,
  input  in_11,
  input  in_12,
  input  in_13,
  input  in_14,
  input  in_15,
  input  in_16,
  input  in_17,
  input  in_18,
  input  in_19,
  input  in_20,
  input  in_21,
  input  C,
  input  in_23,
  input  in_24,
  output out_25,
  output out_26,
  output W,
  output Z,
  output out_29,
  output out_30,
  output out_31,
  output out_32,
  output out_33,
  output out_34
);

  wire transistor_7_out, transistor_10_out, transistor_15_out, transistor_18_out, transistor_20_out,
       transistor_22_out, transistor_26_out, transistor_27_out;

  Pull_Resistor #(.pull(1)) pull_resistor_1 (.node(Z));
  Transistor #(.\type ("n")) transistor_1 (.in(1'b0), .out(Z), .gate(A));
  Pull_Resistor #(.pull(1)) pull_resistor_2 (.node(out_30));
  Transistor #(.\type ("n")) transistor_2 (.in(1'b0), .out(out_30), .gate(C));
  Transistor #(.\type ("n")) transistor_3 (.in(1'b0), .out(W), .gate(X));
  Pull_Resistor #(.pull(1)) pull_resistor_3 (.node(W));
  Transistor #(.\type ("n")) transistor_4 (.in(1'b0), .out(W), .gate(Y));
  Transistor transistor_5 (.in(in_13), .out(out_32), .gate(in_19));
  Transistor #(.\type ("n")) transistor_6 (.in(1'b0), .out(out_32), .gate(in_19));
  Transistor #(.\type ("n")) transistor_7 (.in(1'b0), .out(transistor_7_out), .gate(in_4));
  Pull_Resistor #(.pull(1)) pull_resistor_4 (.node(transistor_7_out));
  Transistor #(.\type ("n")) transistor_8 (.in(1'b0), .out(transistor_7_out), .gate(in_7));
  Pull_Resistor #(.pull(1)) pull_resistor_5 (.node(out_26));
  Transistor #(.\type ("n")) transistor_9 (.in(1'b0), .out(out_26), .gate(transistor_7_out));
  Transistor transistor_10 (.in(in_8), .out(transistor_10_out), .gate(in_15));
  Transistor transistor_11 (.in(transistor_10_out), .out(out_29), .gate(in_23));
  Transistor #(.\type ("n")) transistor_12 (.in(1'b0), .out(out_29), .gate(in_15));
  Transistor #(.\type ("n")) transistor_13 (.in(1'b0), .out(out_29), .gate(in_23));
  Pull_Resistor #(.pull(1)) pull_resistor_6 (.node(out_25));
  Transistor #(.\type ("n")) transistor_14 (.in(transistor_15_out), .out(out_25), .gate(in_1));
  Transistor #(.\type ("n")) transistor_15 (.in(1'b0), .out(transistor_15_out), .gate(in_5));
  Transistor transistor_16 (.in(in_9), .out(out_34), .gate(in_17));
  Transistor #(.\type ("n")) transistor_17 (.in(transistor_18_out), .out(out_34), .gate(in_17));
  Transistor #(.\type ("n")) transistor_18 (.in(1'b0), .out(transistor_18_out), .gate(in_20));
  Transistor transistor_19 (.in(in_9), .out(out_34), .gate(in_20));
  Transistor transistor_20 (.in(in_10), .out(transistor_20_out), .gate(in_18));
  Transistor #(.\type ("n")) transistor_21 (.in(transistor_22_out), .out(transistor_20_out), .gate(in_18));
  Transistor #(.\type ("n")) transistor_22 (.in(1'b0), .out(transistor_22_out), .gate(in_21));
  Transistor transistor_23 (.in(in_10), .out(transistor_20_out), .gate(in_21));
  Transistor transistor_24 (.in(in_14), .out(out_33), .gate(transistor_20_out));
  Transistor #(.\type ("n")) transistor_25 (.in(1'b0), .out(out_33), .gate(transistor_20_out));
  Transistor #(.\type ("n")) transistor_26 (.in(1'b0), .out(transistor_26_out), .gate(in_16));
  Transistor transistor_27 (.in(in_11), .out(transistor_27_out), .gate(in_16));
  Transistor transistor_28 (.in(transistor_27_out), .out(transistor_26_out), .gate(in_24));
  Transistor #(.\type ("n")) transistor_29 (.in(1'b0), .out(transistor_26_out), .gate(in_24));
  Transistor transistor_30 (.in(in_12), .out(out_31), .gate(transistor_26_out));
  Transistor #(.\type ("n")) transistor_31 (.in(1'b0), .out(out_31), .gate(transistor_26_out));

  // Notes on the sheet:
  //   NMOS
  //   Inverter
  //   NOR GATE
  //   Inverter
  //   OR GATE
  //   NOR
  //   NAND
  //   NAND
  //   AND
  //   OR
endmodule

module Adder_1_bit (
  input  A,
  input  B,
  input  Cin,
  output S,
  output Co
);

  wire and_1_out, and_2_out, xor_1_out;

  xor xor_1 (xor_1_out, A, B);
  xor xor_2 (S, xor_1_out, Cin);
  and and_1 (and_1_out, xor_1_out, Cin);
  and and_2 (and_2_out, A, B);
  or or_1 (Co, and_1_out, and_2_out);

  // Notes on the sheet:
  //   1-Bit Full Adder
endmodule

module ADDER_4_bit (
  input  [3:0] B,
  input  [3:0] A,
  output [3:0] S,
  output Co
);

  wire FA1_co, FA2_co, FA3_co;

  Adder_1_bit FA4 (.A(A[3]), .B(B[3]), .Cin(FA3_co), .S(S[3]), .Co(Co));
  Adder_1_bit FA3 (.A(A[2]), .B(B[2]), .Cin(FA2_co), .S(S[2]), .Co(FA3_co));
  Adder_1_bit FA2 (.A(A[1]), .B(B[1]), .Cin(FA1_co), .S(S[1]), .Co(FA2_co));
  Adder_1_bit FA1 (.A(A[0]), .B(B[0]), .Cin(1'b0), .S(S[0]), .Co(FA1_co));

  // Notes on the sheet:
  //   4-Bit Full Adder Using 1-Bit Full Adder
endmodule

module Adder_8_bit (
  input  [3:0] B1,
  input  [3:0] B2,
  input  [3:0] A1,
  input  [3:0] A2,
  input  in_5,
  output Co,
  output [3:0] Z1,
  output [3:0] Z2
);

  // ADDER_4_bit adder_4_bit_1: pin names not known; wires that end beside it: Z1, Z1
  // ADDER_4_bit adder_4_bit_2: pin names not known; wires that end beside it: Z2, Z2

  // Notes on the sheet:
  //   8-Bit Full Adder Using 4-Bit Full Adder
endmodule

module ALU_4bit (
  input  [3:0] A,
  input  [3:0] B,
  input  [3:0] OP,
  output CF,
  output [3:0] R,
  output SF,
  output ZF
);

  wire [3:0] ADD, AND4bit, LR_4bit, LS_4bit, NOT4bit, OR4bit, RR_4bit, RS_4bit, XOR4bit;

  ADDER_4_bit adder_4_bit_1 (.B(B), .A(A), .S(ADD), .Co(CF));
  AND_4_bit and_4_bit_1 (.B(B), .A(A), .R(AND4bit));
  OR_4_bit or_4_bit_1 (.B(B), .A(A), .R(OR4bit));
  XOR_4_bit xor_4_bit_1 (.B(B), .A(A), .R(XOR4bit));
  NOT_4_bit not_4_bit_1 (.A(A), .R(NOT4bit));
  Right_Shift right_shift_1 (.B(B[1:0]), .A(A), .R(RS_4bit));
  Left_Shift left_shift_1 (.B(B[1:0]), .A(A), .R(LS_4bit));
  Right_Rotate right_rotate_1 (.B(B[1:0]), .A(A), .R(RR_4bit));
  Left_Rotate left_rotate_1 (.B(B[1:0]), .A(A), .R(LR_4bit));
  Multiplexer #(.select(4), .width(4)) multiplexer_1 (
    .in0(AND4bit), .in1(OR4bit), .in2(XOR4bit), .in3(LS_4bit), .in4(RS_4bit), .in5(ADD), .in6(LR_4bit),
    .in7(RR_4bit), .in8(NOT4bit), .out(R), .sel(OP));  // open: in9, in10, in11, in12, in13, in14, in15
  nor nor_1 (ZF, R[0], R[1], R[2], R[3]);

  assign SF = R[3];

  // Other names for the same wires on the sheet: Sel[1:0] = B[1:0]
endmodule

module AND_4_bit (
  input  [3:0] B,
  input  [3:0] A,
  output [3:0] R
);

  and and_1 (R[3], A[3], B[3]);
  and and_2 (R[2], A[2], B[2]);
  and and_3 (R[1], A[1], B[1]);
  and and_4 (R[0], A[0], B[0]);
endmodule

module Right_Shift (
  input  [1:0] B,
  input  [3:0] A,
  output [3:0] R
);

  Multiplexer #(.select(2)) multiplexer_1 (.in0(A[3]), .in1(1'b0), .in2(1'b0), .in3(1'b0), .out(R[3]), .sel(B));
  Multiplexer #(.select(2)) multiplexer_2 (.in0(A[2]), .in1(A[3]), .in2(1'b0), .in3(1'b0), .out(R[2]), .sel(B));
  Multiplexer #(.select(2)) multiplexer_3 (.in0(A[1]), .in1(A[2]), .in2(A[3]), .in3(1'b0), .out(R[1]), .sel(B));
  Multiplexer #(.select(2)) multiplexer_4 (.in0(A[0]), .in1(A[1]), .in2(A[2]), .in3(A[3]), .out(R[0]), .sel(B));
endmodule

module Left_Shift (
  input  [1:0] B,
  input  [3:0] A,
  output [3:0] R
);

  Multiplexer #(.select(2)) multiplexer_1 (.in0(A[3]), .in1(A[2]), .in2(A[1]), .in3(A[0]), .out(R[3]), .sel(B));
  Multiplexer #(.select(2)) multiplexer_2 (.in0(A[2]), .in1(A[1]), .in2(A[0]), .in3(1'b0), .out(R[2]), .sel(B));
  Multiplexer #(.select(2)) multiplexer_3 (.in0(A[1]), .in1(A[0]), .in2(1'b0), .in3(1'b0), .out(R[1]), .sel(B));
  Multiplexer #(.select(2)) multiplexer_4 (.in0(A[0]), .in1(1'b0), .in2(1'b0), .in3(1'b0), .out(R[0]), .sel(B));
endmodule

module Right_Rotate (
  input  [1:0] B,
  input  [3:0] A,
  output [3:0] R
);

  Multiplexer #(.select(2)) multiplexer_1 (.in0(A[3]), .in1(A[0]), .in2(A[1]), .in3(A[2]), .out(R[3]), .sel(B));
  Multiplexer #(.select(2)) multiplexer_2 (.in0(A[2]), .in1(A[3]), .in2(A[0]), .in3(A[1]), .out(R[2]), .sel(B));
  Multiplexer #(.select(2)) multiplexer_3 (.in0(A[1]), .in1(A[2]), .in2(A[3]), .in3(A[0]), .out(R[1]), .sel(B));
  Multiplexer #(.select(2)) multiplexer_4 (.in0(A[0]), .in1(A[1]), .in2(A[2]), .in3(A[3]), .out(R[0]), .sel(B));
endmodule

module Left_Rotate (
  input  [1:0] B,
  input  [3:0] A,
  output [3:0] R
);

  Multiplexer #(.select(2)) multiplexer_1 (.in0(A[3]), .in1(A[2]), .in2(A[1]), .in3(A[0]), .out(R[3]), .sel(B));
  Multiplexer #(.select(2)) multiplexer_2 (.in0(A[2]), .in1(A[1]), .in2(A[0]), .in3(A[3]), .out(R[2]), .sel(B));
  Multiplexer #(.select(2)) multiplexer_3 (.in0(A[1]), .in1(A[0]), .in2(A[3]), .in3(A[2]), .out(R[1]), .sel(B));
  Multiplexer #(.select(2)) multiplexer_4 (.in0(A[0]), .in1(A[3]), .in2(A[2]), .in3(A[1]), .out(R[0]), .sel(B));
endmodule

module OR_4_bit (
  input  [3:0] B,
  input  [3:0] A,
  output [3:0] R
);

  or or_1 (R[3], A[3], B[3]);
  or or_2 (R[2], A[2], B[2]);
  or or_3 (R[1], A[1], B[1]);
  or or_4 (R[0], A[0], B[0]);
endmodule

module XOR_4_bit (
  input  [3:0] B,
  input  [3:0] A,
  output [3:0] R
);

  xor xor_1 (R[3], A[3], B[3]);
  xor xor_2 (R[2], A[2], B[2]);
  xor xor_3 (R[1], A[1], B[1]);
  xor xor_4 (R[0], A[0], B[0]);
endmodule

module NOT_4_bit (
  input  [3:0] A,
  output [3:0] R
);

  not not_1 (R[3], A[3]);
  not not_2 (R[2], A[2]);
  not not_3 (R[1], A[1]);
  not not_4 (R[0], A[0]);
endmodule

module TEST (
  input  [3:0] B,
  input  [3:0] A,
  input  [3:0] OP,
  output [3:0] R,
  output CF,
  output SF,
  output ZF
);

  ALU_4bit alu_4bit_1 (.OP(OP), .A(A), .B(B), .R(R), .SF(SF), .CF(CF), .ZF(ZF));
endmodule
