// Logisim project LPE2_2003154_Q1.circ as structural Verilog: 3 circuits, main circuit xor3bit
module xor3bit (
  input  [2:0] A,
  input  [2:0] B,
  output [2:0] R
);

  xor xor_1 (R[0], A[0], B[0]);
  xor xor_2 (R[1], A[1], B[1]);
  xor xor_3 (R[2], A[2], B[2]);
endmodule

module leftshift3bit (
  input  [2:0] A,
  input  [2:0] B,
  output [2:0] R
);

  Multiplexer #(.select(3)) multiplexer_1 (
    .in0(A[2]), .in1(A[1]), .in2(A[0]), .in3(1'b0), .in4(1'b0), .out(R[2]), .sel(B));  // open: in5, in6, in7
  Multiplexer #(.select(3)) multiplexer_2 (
    .in0(A[1]), .in1(A[0]), .in2(1'b0), .in3(1'b0), .in4(1'b0), .out(R[1]), .sel(B));  // open: in5, in6, in7
  Multiplexer #(.select(3)) multiplexer_3 (
    .in0(A[0]), .in1(1'b0), .in2(1'b0), .in3(1'b0), .in4(1'b0), .out(R[0]), .sel(B));  // open: in5, in6, in7

  // Other names for the same wires on the sheet: Shift[2:0] = B
endmodule

module alu3bit (
  input  [1:0] Op,
  input  [2:0] A,
  input  [2:0] B,
  output [2:0] R,
  output Sign_flag,
  output Zero_flag
);

  wire or_1_out;
  wire [2:0] Left_shift, Xorr;

  xor3bit xor3bit_1 (.A(A), .B(B), .R(Xorr));
  leftshift3bit leftshift3bit_1 (.A(A), .B(B), .R(Left_shift));
  Multiplexer #(.select(2), .width(3)) multiplexer_1 (
    .in0(Left_shift), .in3(Xorr), .out(R), .sel(Op));  // open: in1, in2
  or or_1 (or_1_out, R[0], R[1], R[2]);
  not not_1 (Zero_flag, or_1_out);

  assign Sign_flag = R[2];
endmodule
