// Logisim project Register_Set_Library.circ as structural Verilog: 7 circuits, main circuit L_1_bit_Register_2cb9b16a
module L_1_bit_Register_2cb9b16a (
  input  Din,
  input  Sel,
  input  Clock,
  output Dout
);

  wire l_1_bit_2to1_mux_4d3543a6_1_out;

  L_1_bit_2to1_MUX_4d3543a6 l_1_bit_2to1_mux_4d3543a6_1 (
    .A(Dout), .Sel(Sel), .B(Din), .Out(l_1_bit_2to1_mux_4d3543a6_1_out));
  D_Flip_Flop d_ff_1 (.D(l_1_bit_2to1_mux_4d3543a6_1_out), .clk(Clock), .Q(Dout));  // open: Qn, preset, reset
endmodule

module L_1_bit_2to1_MUX_4d3543a6 (
  input  A,
  input  Sel,
  input  B,
  output Out
);

  wire and_1_out, and_2_out, not_1_out;

  not not_1 (not_1_out, Sel);
  and and_1 (and_1_out, A, not_1_out);
  and and_2 (and_2_out, Sel, B);
  or or_1 (Out, and_1_out, and_2_out);
endmodule

module L_8_bit_Register_73bd68cf (
  input  [7:0] Din_7_0_775ea691,
  input  Sel,
  input  Clock,
  output [7:0] Dout_7_0_2210bf5e
);

  L_1_bit_Register_2cb9b16a l_1_bit_register_2cb9b16a_1 (
    .Din(Din_7_0_775ea691[7]), .Sel(Sel), .Clock(Clock), .Dout(Dout_7_0_2210bf5e[7]));
  L_1_bit_Register_2cb9b16a l_1_bit_register_2cb9b16a_2 (
    .Din(Din_7_0_775ea691[6]), .Sel(Sel), .Clock(Clock), .Dout(Dout_7_0_2210bf5e[6]));
  L_1_bit_Register_2cb9b16a l_1_bit_register_2cb9b16a_3 (
    .Din(Din_7_0_775ea691[5]), .Sel(Sel), .Clock(Clock), .Dout(Dout_7_0_2210bf5e[5]));
  L_1_bit_Register_2cb9b16a l_1_bit_register_2cb9b16a_4 (
    .Din(Din_7_0_775ea691[4]), .Sel(Sel), .Clock(Clock), .Dout(Dout_7_0_2210bf5e[4]));
  L_1_bit_Register_2cb9b16a l_1_bit_register_2cb9b16a_5 (
    .Din(Din_7_0_775ea691[3]), .Sel(Sel), .Clock(Clock), .Dout(Dout_7_0_2210bf5e[3]));
  L_1_bit_Register_2cb9b16a l_1_bit_register_2cb9b16a_6 (
    .Din(Din_7_0_775ea691[2]), .Sel(Sel), .Clock(Clock), .Dout(Dout_7_0_2210bf5e[2]));
  L_1_bit_Register_2cb9b16a l_1_bit_register_2cb9b16a_7 (
    .Din(Din_7_0_775ea691[1]), .Sel(Sel), .Clock(Clock), .Dout(Dout_7_0_2210bf5e[1]));
  L_1_bit_Register_2cb9b16a l_1_bit_register_2cb9b16a_8 (
    .Din(Din_7_0_775ea691[0]), .Sel(Sel), .Clock(Clock), .Dout(Dout_7_0_2210bf5e[0]));
endmodule

module L_4_bit_Register_16314f6f (
  input  [3:0] Din_3_0_44858e1c,
  input  Sel,
  input  Clock,
  output [3:0] Dout_3_0_246d7d7f
);

  L_1_bit_Register_2cb9b16a l_1_bit_register_2cb9b16a_1 (
    .Din(Din_3_0_44858e1c[0]), .Sel(Sel), .Clock(Clock), .Dout(Dout_3_0_246d7d7f[0]));
  L_1_bit_Register_2cb9b16a l_1_bit_register_2cb9b16a_2 (
    .Din(Din_3_0_44858e1c[1]), .Sel(Sel), .Clock(Clock), .Dout(Dout_3_0_246d7d7f[1]));
  L_1_bit_Register_2cb9b16a l_1_bit_register_2cb9b16a_3 (
    .Din(Din_3_0_44858e1c[2]), .Sel(Sel), .Clock(Clock), .Dout(Dout_3_0_246d7d7f[2]));
  L_1_bit_Register_2cb9b16a l_1_bit_register_2cb9b16a_4 (
    .Din(Din_3_0_44858e1c[3]), .Sel(Sel), .Clock(Clock), .Dout(Dout_3_0_246d7d7f[3]));
endmodule

module Register_Set_with_8_4_bit_Registers_54003e8c (
  input  REG_EN,
  input  [2:0] Wr,
  input  [3:0] Wrd,
  input  [3:0] Input_Data,
  input  Input_EN,
  input  Clock,
  input  [2:0] Ra,
  input  [2:0] Rb,
  output [3:0] A,
  output [3:0] B,
  output [3:0] Output_Data
);

  wire Reg0, Reg1, Reg2, Reg3, Reg4, Reg5, Reg6;
  wire [3:0] R0, R1, R2, R3, R4, R5, R7;

  Decoder #(.select(3)) decoder_1 (
    .out0(Reg0), .out1(Reg1), .out2(Reg2), .out3(Reg3), .out4(Reg4), .out5(Reg5), .out6(Reg6), .sel(Wr),
    .en(REG_EN));  // open: out7
  L_4_bit_Register_16314f6f Register_0 (.Sel(Reg0), .Clock(Clock), .Din_3_0_44858e1c(Wrd), .Dout_3_0_246d7d7f(R0));
  L_4_bit_Register_16314f6f Register_1 (.Sel(Reg1), .Clock(Clock), .Din_3_0_44858e1c(Wrd), .Dout_3_0_246d7d7f(R1));
  L_4_bit_Register_16314f6f Register_2 (.Sel(Reg2), .Clock(Clock), .Din_3_0_44858e1c(Wrd), .Dout_3_0_246d7d7f(R2));
  L_4_bit_Register_16314f6f Register_3 (.Sel(Reg3), .Clock(Clock), .Din_3_0_44858e1c(Wrd), .Dout_3_0_246d7d7f(R3));
  L_4_bit_Register_16314f6f Register_4 (.Sel(Reg4), .Clock(Clock), .Din_3_0_44858e1c(Wrd), .Dout_3_0_246d7d7f(R4));
  L_4_bit_Register_16314f6f STACK_REGISTER (.Sel(Reg5), .Clock(Clock), .Din_3_0_44858e1c(Wrd), .Dout_3_0_246d7d7f(R5));
  L_4_bit_Register_16314f6f OUTPUT_REGISTER (
    .Sel(Reg6), .Clock(Clock), .Din_3_0_44858e1c(Wrd), .Dout_3_0_246d7d7f(Output_Data));
  L_4_bit_Register_16314f6f INPUT_REGISTER (
    .Sel(Input_EN), .Clock(Clock), .Din_3_0_44858e1c(Input_Data), .Dout_3_0_246d7d7f(R7));
  Multiplexer #(.select(3), .width(4)) multiplexer_1 (
    .in0(R0), .in1(R1), .in2(R2), .in3(R3), .in4(R4), .in5(R5), .in6(Output_Data), .in7(R7), .out(A), .sel(Ra));
  Multiplexer #(.select(3), .width(4)) multiplexer_2 (
    .in0(R0), .in1(R1), .in2(R2), .in3(R3), .in4(R4), .in5(R5), .in6(Output_Data), .in7(R7), .out(B), .sel(Rb));

  // Other names for the same wires on the sheet: R6[3:0] = Output_Data
endmodule

module FLAG_Register_69780251 (
  input  CF,
  input  in_2,
  input  in_3,
  input  Clock,
  output out_5,
  output SF,
  output ZF
);

  L_1_bit_Register_2cb9b16a l_1_bit_register_2cb9b16a_1 (.Din(CF), .Sel(1'b1), .Clock(Clock), .Dout(out_5));
  L_1_bit_Register_2cb9b16a l_1_bit_register_2cb9b16a_2 (.Din(in_2), .Sel(1'b1), .Clock(Clock), .Dout(SF));
  L_1_bit_Register_2cb9b16a l_1_bit_register_2cb9b16a_3 (.Din(in_3), .Sel(1'b1), .Clock(Clock), .Dout(ZF));
endmodule

module Register_Set_Testing (
  input  [2:0] Ra_2_0_575cf57e,
  input  [2:0] Rb_2_0_bdb859de,
  input  REG_EN,
  input  [2:0] Wr_2_0_da3390fe,
  input  [3:0] Wrd_3_0_0dbffd9e,
  input  [3:0] InputR_Data_3_0_70f35ebe,
  input  InputR_Enable_ee34e34b,
  output [3:0] OutputR_Data_3_0_cb2ccc5b,
  output [3:0] A_3_0_c99e8315,
  output [3:0] B_3_0_52fb61dc
);

  wire clock_1_out;

  Clock clock_1 (.out(clock_1_out));
  Register_Set_with_8_4_bit_Registers_54003e8c register_set_with_8_4_bit_registers_54003e8c_1 (
    .Input_EN(InputR_Enable_ee34e34b), .Clock(clock_1_out), .Ra(Ra_2_0_575cf57e), .Rb(Rb_2_0_bdb859de),
    .REG_EN(REG_EN), .Wr(Wr_2_0_da3390fe), .Wrd(Wrd_3_0_0dbffd9e), .Input_Data(InputR_Data_3_0_70f35ebe),
    .B(B_3_0_52fb61dc), .Output_Data(OutputR_Data_3_0_cb2ccc5b), .A(A_3_0_c99e8315));
endmodule
