// Logisim project Priority_Encoder.circ as structural Verilog: 1 circuit, main circuit main
module main (
  input  D3,
  input  D2,
  input  D1,
  input  D0,
  output A0,
  output A1
);

  wire and_1_out, and_2_out, not_1_out, not_2_out;

  not not_1 (not_1_out, D3);
  not not_2 (not_2_out, D2);
  and and_1 (and_1_out, D1, not_2_out, not_1_out);
  and and_2 (and_2_out, not_1_out, D2);
  or or_1 (A0, D3, and_1_out);
  or or_2 (A1, D3, and_2_out);
endmodule
