// Logisim project de_coder.circ as structural Verilog: 1 circuit, main circuit main
module main (
  input  B,
  input  A,
  input  E,
  output D0,
  output D1,
  output D2,
  output D3
);

  wire not_1_out, not_2_out;

  not not_1 (not_1_out, A);
  not not_2 (not_2_out, B);
  and and_1 (D0, E, not_1_out, not_2_out);
  and and_2 (D1, E, not_1_out, B);
  and and_3 (D2, E, A, not_2_out);
  and and_4 (D3, E, A, B);

  // Notes on the sheet:
  //   2 to 4 Decoder
endmodule
